// Digital circuit adder_4bits_copy.dig as structural Verilog
module adder_4bits_copy (
  input  in_c,
  input  in_3,
  input  in_2,
  input  in_1,
  input  in_0,
  output out_c,
  output out_1,
  output out_0,
  output out_2,
  output out_3
);

  wire and_1_out, and_2_out, and_3_out;

  and and_1 (and_1_out, in_0, in_c);
  and and_2 (and_2_out, in_0, in_1, in_c);
  and and_3 (and_3_out, in_0, in_1, in_2, in_c);
  and and_4 (out_c, in_0, in_1, in_2, in_3, in_c);
  half_adder half_adder_1 (.b(in_c), .a(in_0), .Result(out_0));  // open: CarryOut
  half_adder half_adder_2 (.b(and_1_out), .a(in_1), .Result(out_1));  // open: CarryOut
  half_adder half_adder_3 (.b(and_2_out), .a(in_2), .Result(out_2));  // open: CarryOut
  half_adder half_adder_4 (.b(and_3_out), .a(in_3), .Result(out_3));  // open: CarryOut
endmodule
