// Digital circuit multiplexer.dig as structural Verilog
module multiplexer (
  input  Input_0,
  input  Input_1,
  input  Select,
  output Output
);

  Multiplexer multiplexer_1 (.sel(Select), .in_0(Input_0), .in_1(Input_1), .out(Output));
endmodule
