// Digital circuit twos_complement_dq_copy.dig as structural Verilog
module twos_complement_dq_copy (
  input  s_7,
  input  s_6,
  input  s_5,
  input  s_4,
  input  s_3,
  input  s_2,
  input  s_1,
  input  s_0,
  output c_7,
  output c_6,
  output c_5,
  output c_4,
  output c_3,
  output c_2,
  output c_1,
  output c_0
);

  wire adder_4bits_copy_2_out_c, multiplexer_1_out, multiplexer_2_out, multiplexer_3_out, multiplexer_4_out,
       multiplexer_5_out, multiplexer_6_out, multiplexer_7_out, not_1_out, not_2_out, not_3_out, not_4_out,
       not_5_out, not_6_out, not_7_out;

  not not_1 (not_1_out, s_6);
  Multiplexer multiplexer_1 (.sel(s_7), .in_0(s_6), .in_1(not_1_out), .out(multiplexer_1_out));
  not not_2 (not_2_out, s_5);
  adder_4bits_copy adder_4bits_copy_1 (
    .in_c(adder_4bits_copy_2_out_c), .in_0(multiplexer_3_out), .in_1(multiplexer_2_out),
    .in_2(multiplexer_1_out), .in_3(1'b0), .out_0(c_4), .out_1(c_5), .out_2(c_6));  // open: out_c, out_3
  Multiplexer multiplexer_2 (.sel(s_7), .in_0(s_5), .in_1(not_2_out), .out(multiplexer_2_out));
  not not_3 (not_3_out, s_4);
  Multiplexer multiplexer_3 (.sel(s_7), .in_0(s_4), .in_1(not_3_out), .out(multiplexer_3_out));
  not not_4 (not_4_out, s_3);
  Multiplexer multiplexer_4 (.sel(s_7), .in_0(s_3), .in_1(not_4_out), .out(multiplexer_4_out));
  not not_5 (not_5_out, s_2);
  Multiplexer multiplexer_5 (.sel(s_7), .in_0(s_2), .in_1(not_5_out), .out(multiplexer_5_out));
  adder_4bits_copy adder_4bits_copy_2 (
    .in_c(s_7), .in_0(multiplexer_7_out), .in_1(multiplexer_6_out), .in_2(multiplexer_5_out),
    .in_3(multiplexer_4_out), .out_c(adder_4bits_copy_2_out_c), .out_0(c_0), .out_1(c_1), .out_2(c_2),
    .out_3(c_3));
  not not_6 (not_6_out, s_1);
  Multiplexer multiplexer_6 (.sel(s_7), .in_0(s_1), .in_1(not_6_out), .out(multiplexer_6_out));
  not not_7 (not_7_out, s_0);
  Multiplexer multiplexer_7 (.sel(s_7), .in_0(s_0), .in_1(not_7_out), .out(multiplexer_7_out));

  assign c_7 = s_7;

  // Notes on the sheet:
  //   Sign-magnitude representation
  //   Two's complement
endmodule

/* Test case:
s_7 s_6 s_5 s_4 s_3 s_2 s_1 s_0 c_7 c_6 c_5 c_4 c_3 c_2 c_1 c_0
0   0   0   0   0   0   0   1   0   0   0   0   0   0   0   1
0   0   0   0   0   0   1   0   0   0   0   0   0   0   1   0
0   0   0   0   0   1   0   0   0   0   0   0   0   1   0   0
0   0   0   0   1   0   0   0   0   0   0   0   1   0   0   0
0   0   0   1   0   0   0   0   0   0   0   1   0   0   0   0
0   0   1   0   0   0   0   0   0   0   1   0   0   0   0   0
0   1   0   0   0   0   0   0   0   1   0   0   0   0   0   0
1   0   0   0   0   0   0   0   1   0   0   0   0   0   0   0
1   1   1   1   1   1   1   1   1   0   0   0   0   0   0   1
0   1   1   1   1   1   1   1   0   1   1   1   1   1   1   1
1   1   0   0   0   0   0   1   1   0   1   1   1   1   1   1
1   0   1   0   1   0   1   0   1   1   0   1   0   1   1   0
1   0   0   1   0   0   1   0   1   1   1   0   1   1   1   0
*/
