// Digital circuit twos_complement_dq_copy_delay.dig as structural Verilog
module twos_complement_dq_copy_delay (
  input  s_7,
  input  s_6,
  input  s_5,
  input  s_4,
  input  s_3,
  input  s_2,
  input  s_1,
  input  s_0,
  output c_7,
  output c_6,
  output c_5,
  output c_4,
  output c_3,
  output c_2,
  output c_1,
  output c_0
);

  wire adder_4bits_copy_delay_1_o_0, adder_4bits_copy_delay_1_o_1, adder_4bits_copy_delay_1_o_2,
       adder_4bits_copy_delay_2_o_0, adder_4bits_copy_delay_2_o_1, adder_4bits_copy_delay_2_o_2,
       adder_4bits_copy_delay_2_o_3, adder_4bits_copy_delay_2_o_c, delay_1_out, delay_2_out, delay_3_out,
       delay_4_out, delay_5_out, delay_6_out, delay_7_out, delay_8_out, delay_17_out, delay_18_out,
       delay_19_out, delay_20_out, delay_21_out, delay_22_out, delay_23_out, delay_24_out, delay_25_out,
       delay_26_out, delay_27_out, delay_28_out, delay_29_out, delay_30_out, multiplexer_1_out,
       multiplexer_2_out, multiplexer_3_out, multiplexer_4_out, multiplexer_5_out, multiplexer_6_out,
       multiplexer_7_out, not_1_out, not_2_out, not_3_out, not_4_out, not_5_out, not_6_out, not_7_out;

  Delay delay_1 (.in(s_7), .out(delay_1_out));
  Delay delay_2 (.in(s_6), .out(delay_2_out));
  Delay delay_3 (.in(s_5), .out(delay_3_out));
  Delay delay_4 (.in(s_4), .out(delay_4_out));
  Delay delay_5 (.in(s_3), .out(delay_5_out));
  Delay delay_6 (.in(s_2), .out(delay_6_out));
  Delay delay_7 (.in(s_1), .out(delay_7_out));
  Delay delay_8 (.in(s_0), .out(delay_8_out));
  Delay delay_9 (.in(delay_1_out), .out(c_7));
  Delay delay_10 (.in(adder_4bits_copy_delay_1_o_2), .out(c_6));
  Delay delay_11 (.in(adder_4bits_copy_delay_1_o_1), .out(c_5));
  Delay delay_12 (.in(adder_4bits_copy_delay_1_o_0), .out(c_4));
  Delay delay_13 (.in(adder_4bits_copy_delay_2_o_3), .out(c_3));
  Delay delay_14 (.in(adder_4bits_copy_delay_2_o_2), .out(c_2));
  Delay delay_15 (.in(adder_4bits_copy_delay_2_o_1), .out(c_1));
  Delay delay_16 (.in(adder_4bits_copy_delay_2_o_0), .out(c_0));
  not not_1 (not_1_out, delay_2_out);
  Delay delay_17 (.in(not_1_out), .out(delay_17_out));
  Multiplexer multiplexer_1 (.sel(delay_1_out), .in_0(delay_2_out), .in_1(delay_17_out), .out(multiplexer_1_out));
  Delay #(.delayTime(2)) delay_18 (.in(multiplexer_1_out), .out(delay_18_out));
  not not_2 (not_2_out, delay_3_out);
  Delay delay_19 (.in(not_2_out), .out(delay_19_out));
  adder_4bits_copy_delay adder_4bits_copy_delay_1 (
    .CarryIn(adder_4bits_copy_delay_2_o_c), .a_0(delay_22_out), .a_1(delay_20_out), .a_2(delay_18_out),
    .a_3(1'b0), .o_0(adder_4bits_copy_delay_1_o_0), .o_1(adder_4bits_copy_delay_1_o_1),
    .o_2(adder_4bits_copy_delay_1_o_2));  // open: o_c, o_3
  Multiplexer multiplexer_2 (.sel(delay_1_out), .in_0(delay_3_out), .in_1(delay_19_out), .out(multiplexer_2_out));
  Delay #(.delayTime(2)) delay_20 (.in(multiplexer_2_out), .out(delay_20_out));
  not not_3 (not_3_out, delay_4_out);
  Delay delay_21 (.in(not_3_out), .out(delay_21_out));
  Multiplexer multiplexer_3 (.sel(delay_1_out), .in_0(delay_4_out), .in_1(delay_21_out), .out(multiplexer_3_out));
  Delay #(.delayTime(2)) delay_22 (.in(multiplexer_3_out), .out(delay_22_out));
  not not_4 (not_4_out, delay_5_out);
  Delay delay_23 (.in(not_4_out), .out(delay_23_out));
  Multiplexer multiplexer_4 (.sel(delay_1_out), .in_0(delay_5_out), .in_1(delay_23_out), .out(multiplexer_4_out));
  Delay #(.delayTime(2)) delay_24 (.in(multiplexer_4_out), .out(delay_24_out));
  not not_5 (not_5_out, delay_6_out);
  Delay delay_25 (.in(not_5_out), .out(delay_25_out));
  Multiplexer multiplexer_5 (.sel(delay_1_out), .in_0(delay_6_out), .in_1(delay_25_out), .out(multiplexer_5_out));
  Delay #(.delayTime(2)) delay_26 (.in(multiplexer_5_out), .out(delay_26_out));
  adder_4bits_copy_delay adder_4bits_copy_delay_2 (
    .CarryIn(delay_1_out), .a_0(delay_30_out), .a_1(delay_28_out), .a_2(delay_26_out), .a_3(delay_24_out),
    .o_c(adder_4bits_copy_delay_2_o_c), .o_0(adder_4bits_copy_delay_2_o_0),
    .o_1(adder_4bits_copy_delay_2_o_1), .o_2(adder_4bits_copy_delay_2_o_2), .o_3(adder_4bits_copy_delay_2_o_3));
  not not_6 (not_6_out, delay_7_out);
  Delay delay_27 (.in(not_6_out), .out(delay_27_out));
  Multiplexer multiplexer_6 (.sel(delay_1_out), .in_0(delay_7_out), .in_1(delay_27_out), .out(multiplexer_6_out));
  Delay #(.delayTime(2)) delay_28 (.in(multiplexer_6_out), .out(delay_28_out));
  not not_7 (not_7_out, delay_8_out);
  Delay delay_29 (.in(not_7_out), .out(delay_29_out));
  Multiplexer multiplexer_7 (.sel(delay_1_out), .in_0(delay_8_out), .in_1(delay_29_out), .out(multiplexer_7_out));
  Delay #(.delayTime(2)) delay_30 (.in(multiplexer_7_out), .out(delay_30_out));

  // Notes on the sheet:
  //   Sign-magnitude representation
  //   Two's complement
endmodule

/* Test case:
s_7 s_6 s_5 s_4 s_3 s_2 s_1 s_0 c_7 c_6 c_5 c_4 c_3 c_2 c_1 c_0
0   0   0   0   0   0   0   1   0   0   0   0   0   0   0   1
0   0   0   0   0   0   1   0   0   0   0   0   0   0   1   0
0   0   0   0   0   1   0   0   0   0   0   0   0   1   0   0
0   0   0   0   1   0   0   0   0   0   0   0   1   0   0   0
0   0   0   1   0   0   0   0   0   0   0   1   0   0   0   0
0   0   1   0   0   0   0   0   0   0   1   0   0   0   0   0
0   1   0   0   0   0   0   0   0   1   0   0   0   0   0   0
1   0   0   0   0   0   0   0   1   0   0   0   0   0   0   0
1   1   1   1   1   1   1   1   1   0   0   0   0   0   0   1
0   1   1   1   1   1   1   1   0   1   1   1   1   1   1   1
1   1   0   0   0   0   0   1   1   0   1   1   1   1   1   1
1   0   1   0   1   0   1   0   1   1   0   1   0   1   1   0
1   0   0   1   0   0   1   0   1   1   1   0   1   1   1   0
*/
