// Digital circuit 2-bitADD.dig as structural Verilog
module _2_bitADD (
  input  a_2,
  input  a_1,
  input  signe,
  output s_1,
  output t_1,
  output s_2,
  output t_2,
  output r_1,
  output R_1_2
);

  wire _1_bitadd_1_r1, _1_bitadd_1_r_1, _1_bitadd_1_s_1, _1_bitadd_1_t_1, _1_bitadd_2_r1, _1_bitadd_2_r_1,
       and_1_out, and_2_out, not_1_out, not_2_out;

  _1_bitADD _1_bitadd_1 (
    .a_1(a_2), .signe(1'b0), .s_1(_1_bitadd_1_s_1), .t_1(_1_bitadd_1_t_1), .r_1(_1_bitadd_1_r_1),
    .R1(_1_bitadd_1_r1));
  _1_bitADD _1_bitadd_2 (.a_1(a_1), .signe(signe), .s_1(s_1), .t_1(t_1), .r_1(_1_bitadd_2_r_1), .R1(_1_bitadd_2_r1));
  not not_1 (not_1_out, _1_bitadd_2_r_1);
  not not_2 (not_2_out, _1_bitadd_2_r1);
  Multi_simp multi_simp_1 (
    .s_2(_1_bitadd_1_s_1), .t_2(_1_bitadd_1_t_1), .Nr(not_1_out), .r(_1_bitadd_2_r_1), .out(s_2));
  Multi_simp multi_simp_2 (.s_2(_1_bitadd_1_s_1), .t_2(_1_bitadd_1_t_1), .Nr(not_2_out), .r(_1_bitadd_2_r1), .out(t_2));
  and and_1 (and_1_out, _1_bitadd_2_r_1, _1_bitadd_1_r1);
  and and_2 (and_2_out, _1_bitadd_2_r1, _1_bitadd_1_r1);
  or or_1 (r_1, and_1_out, _1_bitadd_1_r_1);
  or or_2 (R_1_2, _1_bitadd_1_r_1, and_2_out);
  LED led_1 (.in(r_1));
  LED led_2 (.in(s_2));
  LED led_3 (.in(s_1));
endmodule
