// Digital circuit 4-bitADD.dig as structural Verilog
module _4_bitADD (
  input  a_4,
  input  a_3,
  input  a_2,
  input  a_1,
  input  signe,
  output s_1,
  output s_2,
  output s_3,
  output s_4,
  output t_1,
  output t_2,
  output t_3,
  output t_4,
  output r_1,
  output R_1_2
);

  wire _2_bitadd_1_r_1, _2_bitadd_1_r_1_2, _2_bitadd_1_s_1, _2_bitadd_1_s_2, _2_bitadd_1_t_1,
       _2_bitadd_1_t_2, _2_bitadd_2_r_1, _2_bitadd_2_r_1_2, and_1_out, and_2_out, not_1_out, not_2_out;

  _2_bitADD _2_bitadd_1 (
    .a_2(a_4), .a_1(a_3), .signe(1'b0), .s_1(_2_bitadd_1_s_1), .t_1(_2_bitadd_1_t_1), .s_2(_2_bitadd_1_s_2),
    .t_2(_2_bitadd_1_t_2), .r_1(_2_bitadd_1_r_1), .R_1_2(_2_bitadd_1_r_1_2));
  _2_bitADD _2_bitadd_2 (
    .a_2(a_2), .a_1(a_1), .signe(signe), .s_1(s_1), .t_1(t_1), .s_2(s_2), .t_2(t_2), .r_1(_2_bitadd_2_r_1),
    .R_1_2(_2_bitadd_2_r_1_2));
  not not_1 (not_1_out, _2_bitadd_2_r_1);
  not not_2 (not_2_out, _2_bitadd_2_r_1_2);
  Multi_simp multi_simp_1 (
    .s_2(_2_bitadd_1_s_1), .t_2(_2_bitadd_1_t_1), .Nr(not_1_out), .r(_2_bitadd_2_r_1), .out(s_3));
  Multi_simp multi_simp_2 (
    .s_2(_2_bitadd_1_s_2), .t_2(_2_bitadd_1_t_2), .Nr(not_1_out), .r(_2_bitadd_2_r_1), .out(s_4));
  Multi_simp multi_simp_3 (
    .s_2(_2_bitadd_1_s_1), .t_2(_2_bitadd_1_t_1), .Nr(not_2_out), .r(_2_bitadd_2_r_1_2), .out(t_3));
  Multi_simp multi_simp_4 (
    .s_2(_2_bitadd_1_s_2), .t_2(_2_bitadd_1_t_2), .Nr(not_2_out), .r(_2_bitadd_2_r_1_2), .out(t_4));
  and and_1 (and_1_out, _2_bitadd_1_r_1_2, _2_bitadd_2_r_1);
  and and_2 (and_2_out, _2_bitadd_2_r_1_2, _2_bitadd_1_r_1_2);
  or or_1 (r_1, _2_bitadd_1_r_1, and_1_out);
  or or_2 (R_1_2, and_2_out, _2_bitadd_1_r_1);
  LED led_1 (.in(r_1));
  LED led_2 (.in(s_4));
  LED led_3 (.in(s_3));
  LED led_4 (.in(s_2));
  LED led_5 (.in(s_1));
endmodule
