// Digital circuit 8bits_adder.dig as structural Verilog
module _8bits_adder (
  input  a_0,
  input  a_1,
  input  a_2,
  input  a_3,
  input  a_4,
  input  a_5,
  input  a_6,
  input  a_7,
  input  b_0,
  input  b_1,
  input  b_2,
  input  b_3,
  input  b_4,
  input  b_5,
  input  b_6,
  input  b_7,
  output r_1,
  output R_1_2,
  output s_0,
  output s_1,
  output s_2,
  output s_3,
  output t_0,
  output t_1,
  output t_2,
  output t_3,
  output t_4,
  output t_5,
  output t_6,
  output t_7,
  output s_4,
  output s_5,
  output s_6,
  output s_7
);

  wire _4bits_adder_1_r_1, _4bits_adder_1_r_1_2, _4bits_adder_1_s_0, _4bits_adder_1_s_1, _4bits_adder_1_s_2,
       _4bits_adder_1_s_3, _4bits_adder_1_t_0, _4bits_adder_1_t_1, _4bits_adder_1_t_2, _4bits_adder_1_t_3,
       _4bits_adder_2_r_1, _4bits_adder_2_r_1_2, and_1_out, and_2_out, and_3_out, and_4_out, and_5_out,
       and_6_out, and_7_out, and_8_out, and_9_out, and_10_out, and_11_out, and_12_out, and_13_out,
       and_14_out, and_15_out, and_16_out, and_17_out, and_18_out, not_1_out, not_2_out, not_3_out,
       not_4_out, not_5_out, not_6_out, not_7_out, not_8_out;

  _4bits_adder _4bits_adder_1 (
    .a_3(a_7), .a_2(a_6), .a_1(a_5), .a_0(a_4), .b_3(b_7), .b_2(b_6), .b_1(b_5), .b_0(b_4),
    .s_3(_4bits_adder_1_s_3), .s_2(_4bits_adder_1_s_2), .s_1(_4bits_adder_1_s_1), .s_0(_4bits_adder_1_s_0),
    .t_3(_4bits_adder_1_t_3), .t_2(_4bits_adder_1_t_2), .t_1(_4bits_adder_1_t_1), .t_0(_4bits_adder_1_t_0),
    .r_1_2(_4bits_adder_1_r_1_2), .R_1(_4bits_adder_1_r_1));
  _4bits_adder _4bits_adder_2 (
    .a_3(a_3), .a_2(a_2), .a_1(a_1), .a_0(a_0), .b_3(b_3), .b_2(b_2), .b_1(b_1), .b_0(b_0), .s_3(s_3),
    .s_2(s_2), .s_1(s_1), .s_0(s_0), .t_3(t_3), .t_2(t_2), .t_1(t_1), .t_0(t_0),
    .r_1_2(_4bits_adder_2_r_1_2), .R_1(_4bits_adder_2_r_1));
  or or_1 (s_7, and_1_out, and_3_out);
  and and_1 (and_1_out, not_1_out, _4bits_adder_1_s_3);
  not not_1 (not_1_out, _4bits_adder_2_r_1_2);
  not not_2 (not_2_out, _4bits_adder_2_r_1);
  and and_2 (and_2_out, _4bits_adder_1_s_3, not_2_out);
  and and_3 (and_3_out, _4bits_adder_2_r_1_2, _4bits_adder_1_t_3);
  and and_4 (and_4_out, _4bits_adder_1_t_3, _4bits_adder_2_r_1);
  or or_2 (t_7, and_4_out, and_2_out);
  or or_3 (s_6, and_5_out, and_7_out);
  and and_5 (and_5_out, not_3_out, _4bits_adder_1_s_2);
  not not_3 (not_3_out, _4bits_adder_2_r_1_2);
  not not_4 (not_4_out, _4bits_adder_2_r_1);
  and and_6 (and_6_out, _4bits_adder_1_s_2, not_4_out);
  and and_7 (and_7_out, _4bits_adder_2_r_1_2, _4bits_adder_1_t_2);
  and and_8 (and_8_out, _4bits_adder_1_t_2, _4bits_adder_2_r_1);
  or or_4 (t_6, and_8_out, and_6_out);
  or or_5 (s_5, and_9_out, and_11_out);
  and and_9 (and_9_out, not_5_out, _4bits_adder_1_s_1);
  not not_5 (not_5_out, _4bits_adder_2_r_1_2);
  not not_6 (not_6_out, _4bits_adder_2_r_1);
  and and_10 (and_10_out, _4bits_adder_1_s_1, not_6_out);
  and and_11 (and_11_out, _4bits_adder_2_r_1_2, _4bits_adder_1_t_1);
  and and_12 (and_12_out, _4bits_adder_1_t_1, _4bits_adder_2_r_1);
  or or_6 (t_5, and_12_out, and_10_out);
  or or_7 (s_4, and_13_out, and_15_out);
  and and_13 (and_13_out, not_7_out, _4bits_adder_1_s_0);
  not not_7 (not_7_out, _4bits_adder_2_r_1_2);
  not not_8 (not_8_out, _4bits_adder_2_r_1);
  and and_14 (and_14_out, _4bits_adder_1_s_0, not_8_out);
  and and_15 (and_15_out, _4bits_adder_2_r_1_2, _4bits_adder_1_t_0);
  and and_16 (and_16_out, _4bits_adder_1_t_0, _4bits_adder_2_r_1);
  or or_8 (t_4, and_16_out, and_14_out);
  and and_17 (and_17_out, _4bits_adder_1_r_1, _4bits_adder_2_r_1_2);
  and and_18 (and_18_out, _4bits_adder_1_r_1, _4bits_adder_2_r_1);
  or or_9 (r_1, _4bits_adder_1_r_1_2, and_17_out);
  or or_10 (R_1_2, _4bits_adder_1_r_1_2, and_18_out);
endmodule
