// Digital circuit Add2bit.dig as structural Verilog
module Add2bit (
  input  b_2,
  input  a_2,
  input  b_1,
  input  a_1,
  output s_1,
  output t_1,
  output s_2,
  output t_2,
  output r_1,
  output R_1_2
);

  wire add1bit_1_r1, add1bit_1_r_1, add1bit_1_s_1, add1bit_1_t_1, add1bit_2_r1, add1bit_2_r_1, and_1_out,
       and_2_out, not_1_out, not_2_out;

  Add1bit add1bit_1 (
    .a_1(a_2), .b_1(b_2), .s_1(add1bit_1_s_1), .t_1(add1bit_1_t_1), .r_1(add1bit_1_r_1), .R1(add1bit_1_r1));
  Add1bit add1bit_2 (.a_1(a_1), .b_1(b_1), .s_1(s_1), .t_1(t_1), .r_1(add1bit_2_r_1), .R1(add1bit_2_r1));
  not not_1 (not_1_out, add1bit_2_r_1);
  not not_2 (not_2_out, add1bit_2_r1);
  Multi_simp multi_simp_1 (.s_2(add1bit_1_s_1), .t_2(add1bit_1_t_1), .Nr(not_1_out), .r(add1bit_2_r_1), .out(s_2));
  Multi_simp multi_simp_2 (.s_2(add1bit_1_s_1), .t_2(add1bit_1_t_1), .Nr(not_2_out), .r(add1bit_2_r1), .out(t_2));
  and and_1 (and_1_out, add1bit_2_r_1, add1bit_1_r1);
  and and_2 (and_2_out, add1bit_2_r1, add1bit_1_r1);
  or or_1 (r_1, and_1_out, add1bit_1_r_1);
  or or_2 (R_1_2, add1bit_1_r_1, and_2_out);
  LED led_1 (.in(r_1));
  LED led_2 (.in(a_2));
  LED led_3 (.in(b_2));
  LED led_4 (.in(s_2));
  LED led_5 (.in(a_1));
  LED led_6 (.in(b_1));
  LED led_7 (.in(s_1));
endmodule
