// Digital circuit Add4bit.dig as structural Verilog
module Add4bit (
  input  b_4,
  input  a_4,
  input  b_3,
  input  a_3,
  input  b_2,
  input  a_2,
  input  b_1,
  input  a_1,
  output s_1,
  output s_2,
  output s_3,
  output s_4,
  output t_1,
  output t_2,
  output t_3,
  output t_4,
  output r_1,
  output R_1_2
);

  wire add2bit_1_r_1, add2bit_1_r_1_2, add2bit_1_s_1, add2bit_1_s_2, add2bit_1_t_1, add2bit_1_t_2,
       add2bit_2_r_1, add2bit_2_r_1_2, and_1_out, and_2_out, not_1_out, not_2_out;

  LED led_1 (.in(a_3));
  LED led_2 (.in(a_4));
  LED led_3 (.in(b_3));
  LED led_4 (.in(b_4));
  LED led_5 (.in(a_2));
  LED led_6 (.in(b_2));
  LED led_7 (.in(a_1));
  LED led_8 (.in(b_1));
  Add2bit add2bit_1 (
    .b_2(b_4), .a_2(a_4), .b_1(b_3), .a_1(a_3), .s_1(add2bit_1_s_1), .t_1(add2bit_1_t_1),
    .s_2(add2bit_1_s_2), .t_2(add2bit_1_t_2), .r_1(add2bit_1_r_1), .R_1_2(add2bit_1_r_1_2));
  Add2bit add2bit_2 (
    .b_2(b_2), .a_2(a_2), .b_1(b_1), .a_1(a_1), .s_1(s_1), .t_1(t_1), .s_2(s_2), .t_2(t_2),
    .r_1(add2bit_2_r_1), .R_1_2(add2bit_2_r_1_2));
  not not_1 (not_1_out, add2bit_2_r_1);
  not not_2 (not_2_out, add2bit_2_r_1_2);
  Multi_simp multi_simp_1 (.s_2(add2bit_1_s_1), .t_2(add2bit_1_t_1), .Nr(not_1_out), .r(add2bit_2_r_1), .out(s_3));
  Multi_simp multi_simp_2 (.s_2(add2bit_1_s_2), .t_2(add2bit_1_t_2), .Nr(not_1_out), .r(add2bit_2_r_1), .out(s_4));
  Multi_simp multi_simp_3 (.s_2(add2bit_1_s_1), .t_2(add2bit_1_t_1), .Nr(not_2_out), .r(add2bit_2_r_1_2), .out(t_3));
  Multi_simp multi_simp_4 (.s_2(add2bit_1_s_2), .t_2(add2bit_1_t_2), .Nr(not_2_out), .r(add2bit_2_r_1_2), .out(t_4));
  and and_1 (and_1_out, add2bit_1_r_1_2, add2bit_2_r_1);
  and and_2 (and_2_out, add2bit_2_r_1_2, add2bit_1_r_1_2);
  or or_1 (r_1, add2bit_1_r_1, and_1_out);
  or or_2 (R_1_2, and_2_out, add2bit_1_r_1);
  LED led_9 (.in(r_1));
  LED led_10 (.in(s_4));
  LED led_11 (.in(s_3));
  LED led_12 (.in(s_2));
  LED led_13 (.in(s_1));
endmodule
