// Digital circuit Add8bit.dig as structural Verilog
module Add8bit (
  input  b_8,
  input  a_8,
  input  b_7,
  input  a_7,
  input  b_6,
  input  a_6,
  input  b_5,
  input  a_5,
  input  b_4,
  input  a_4,
  input  b_3,
  input  a_3,
  input  b_2,
  input  a_2,
  input  b_1,
  input  a_1,
  output s_1,
  output s_2,
  output s_3,
  output s_4,
  output s_5,
  output s_6,
  output s_7,
  output s_8,
  output t_1,
  output r_1,
  output t_2,
  output t_3,
  output t_4,
  output t_5,
  output t_6,
  output t_7,
  output t_8,
  output R_1_2
);

  wire add4bit_1_r_1, add4bit_1_r_1_2, add4bit_1_s_1, add4bit_1_s_2, add4bit_1_s_3, add4bit_1_s_4,
       add4bit_1_t_1, add4bit_1_t_2, add4bit_1_t_3, add4bit_1_t_4, add4bit_2_r_1, add4bit_2_r_1_2, and_1_out,
       and_2_out, not_1_out, not_2_out;

  LED led_1 (.in(b_8));
  LED led_2 (.in(a_8));
  LED led_3 (.in(b_7));
  LED led_4 (.in(a_7));
  LED led_5 (.in(b_6));
  LED led_6 (.in(b_5));
  LED led_7 (.in(a_6));
  LED led_8 (.in(a_5));
  LED led_9 (.in(b_4));
  LED led_10 (.in(b_3));
  LED led_11 (.in(a_4));
  LED led_12 (.in(a_3));
  LED led_13 (.in(b_2));
  LED led_14 (.in(a_2));
  LED led_15 (.in(b_1));
  LED led_16 (.in(a_1));
  Add4bit add4bit_1 (
    .b_4(b_8), .a_4(a_8), .b_3(b_7), .a_3(a_7), .b_2(b_6), .a_2(a_6), .b_1(b_5), .a_1(a_5),
    .s_1(add4bit_1_s_1), .s_2(add4bit_1_s_2), .s_3(add4bit_1_s_3), .s_4(add4bit_1_s_4), .t_1(add4bit_1_t_1),
    .t_2(add4bit_1_t_2), .t_3(add4bit_1_t_3), .t_4(add4bit_1_t_4), .r_1(add4bit_1_r_1),
    .R_1_2(add4bit_1_r_1_2));
  Add4bit add4bit_2 (
    .b_4(b_4), .a_4(a_4), .b_3(b_3), .a_3(a_3), .b_2(b_2), .a_2(a_2), .b_1(b_1), .a_1(a_1), .s_1(s_1),
    .s_2(s_2), .s_3(s_3), .s_4(s_4), .t_1(t_1), .t_2(t_2), .t_3(t_3), .t_4(t_4), .r_1(add4bit_2_r_1),
    .R_1_2(add4bit_2_r_1_2));
  and and_1 (and_1_out, add4bit_2_r_1, add4bit_1_r_1_2);
  and and_2 (and_2_out, add4bit_1_r_1_2, add4bit_2_r_1_2);
  not not_1 (not_1_out, add4bit_2_r_1);
  not not_2 (not_2_out, add4bit_2_r_1_2);
  or or_1 (r_1, add4bit_1_r_1, and_1_out);
  or or_2 (R_1_2, add4bit_1_r_1, and_2_out);
  Multi_simp multi_simp_1 (.s_2(add4bit_1_s_1), .t_2(add4bit_1_t_1), .Nr(not_1_out), .r(add4bit_2_r_1), .out(s_5));
  Multi_simp multi_simp_2 (.s_2(add4bit_1_s_2), .t_2(add4bit_1_t_2), .Nr(not_1_out), .r(add4bit_2_r_1), .out(s_6));
  Multi_simp multi_simp_3 (.s_2(add4bit_1_s_3), .t_2(add4bit_1_t_3), .Nr(not_1_out), .r(add4bit_2_r_1), .out(s_7));
  Multi_simp multi_simp_4 (.s_2(add4bit_1_s_4), .t_2(add4bit_1_t_4), .Nr(not_1_out), .r(add4bit_2_r_1), .out(s_8));
  Multi_simp multi_simp_5 (.s_2(add4bit_1_s_1), .t_2(add4bit_1_t_1), .Nr(not_2_out), .r(add4bit_2_r_1_2), .out(t_5));
  Multi_simp multi_simp_6 (.s_2(add4bit_1_s_2), .t_2(add4bit_1_t_2), .Nr(not_2_out), .r(add4bit_2_r_1_2), .out(t_6));
  Multi_simp multi_simp_7 (.s_2(add4bit_1_s_3), .t_2(add4bit_1_t_3), .Nr(not_2_out), .r(add4bit_2_r_1_2), .out(t_7));
  Multi_simp multi_simp_8 (.s_2(add4bit_1_s_4), .t_2(add4bit_1_t_4), .Nr(not_2_out), .r(add4bit_2_r_1_2), .out(t_8));
  LED led_17 (.in(r_1));
  LED led_18 (.in(s_8));
  LED led_19 (.in(s_7));
  LED led_20 (.in(s_6));
  LED led_21 (.in(s_5));
  LED led_22 (.in(s_4));
  LED led_23 (.in(s_3));
  LED led_24 (.in(s_2));
  LED led_25 (.in(s_1));
endmodule
