// Digital circuit Asyn.dig as structural Verilog
module Asyn (
  input  Com,
  input  Arr,
  output \Durée 
);

  wire not_1_out;

  not not_1 (not_1_out, Arr);
  and and_1 (\Durée , Com, not_1_out);
endmodule
