// Digital circuit Memoire.dig as structural Verilog
module Memoire (
  input  S_7,
  input  S_6,
  input  S_5,
  input  S_4,
  input  S_3,
  input  S_2,
  input  S_1,
  input  S_0,
  input  Clk,
  input  Changer,
  output M_0,
  output M_1,
  output M_2,
  output M_3,
  output M_4,
  output M_5,
  output M_6,
  output M_7
);

  wire multiplexer_1_out, multiplexer_2_out, multiplexer_3_out, multiplexer_4_out, multiplexer_5_out,
       multiplexer_6_out, multiplexer_7_out, multiplexer_8_out;

  Multiplexer multiplexer_1 (.sel(Changer), .in_0(M_7), .in_1(S_7), .out(multiplexer_1_out));
  Multiplexer multiplexer_2 (.sel(Changer), .in_0(M_6), .in_1(S_6), .out(multiplexer_2_out));
  Multiplexer multiplexer_3 (.sel(Changer), .in_0(M_5), .in_1(S_5), .out(multiplexer_3_out));
  Multiplexer multiplexer_4 (.sel(Changer), .in_0(M_4), .in_1(S_4), .out(multiplexer_4_out));
  Multiplexer multiplexer_5 (.sel(Changer), .in_0(M_3), .in_1(S_3), .out(multiplexer_5_out));
  Multiplexer multiplexer_6 (.sel(Changer), .in_0(M_2), .in_1(S_2), .out(multiplexer_6_out));
  Multiplexer multiplexer_7 (.sel(Changer), .in_0(M_1), .in_1(S_1), .out(multiplexer_7_out));
  Multiplexer multiplexer_8 (.sel(Changer), .in_0(M_0), .in_1(S_0), .out(multiplexer_8_out));
  Memoire_1bit memoire_1bit_1 (.D(multiplexer_1_out), .Clk(Clk), .M(M_7));
  Memoire_1bit memoire_1bit_2 (.D(multiplexer_2_out), .Clk(Clk), .M(M_6));
  Memoire_1bit memoire_1bit_3 (.D(multiplexer_3_out), .Clk(Clk), .M(M_5));
  Memoire_1bit memoire_1bit_4 (.D(multiplexer_4_out), .Clk(Clk), .M(M_4));
  Memoire_1bit memoire_1bit_5 (.D(multiplexer_5_out), .Clk(Clk), .M(M_3));
  Memoire_1bit memoire_1bit_6 (.D(multiplexer_6_out), .Clk(Clk), .M(M_2));
  Memoire_1bit memoire_1bit_7 (.D(multiplexer_7_out), .Clk(Clk), .M(M_1));
  Memoire_1bit memoire_1bit_8 (.D(multiplexer_8_out), .Clk(Clk), .M(M_0));
endmodule
