// Digital circuit Multi_simp.dig as structural Verilog
module Multi_simp (
  input  s_2,
  input  t_2,
  input  Nr,
  input  r,
  output out
);

  wire and_1_out, and_2_out;

  and and_1 (and_1_out, s_2, Nr);
  and and_2 (and_2_out, t_2, r);
  or or_1 (out, and_1_out, and_2_out);
endmodule
