// Digital circuit alu.dig as structural Verilog
module alu (
  input  i_1_bit_0,
  input  i_2_bit_0,
  input  i_1_bit_1,
  input  i_1_bit_2,
  input  i_1_bit_3,
  input  i_1_bit_4,
  input  i_1_bit_5,
  input  i_1_bit_6,
  input  i_1_bit_7,
  input  i_2_bit_1,
  input  i_2_bit_2,
  input  i_2_bit_3,
  input  i_2_bit_4,
  input  i_2_bit_5,
  input  i_2_bit_6,
  input  i_2_bit_7,
  input  Sgn,
  output o_0,
  output o_1,
  output o_2,
  output o_3,
  output o_4,
  output o_5,
  output o_6,
  output o_7
);

  wire multiplexer_1_out, multiplexer_2_out, multiplexer_3_out, multiplexer_4_out, multiplexer_5_out,
       multiplexer_6_out, multiplexer_7_out, multiplexer_8_out, not_1_out, twos_complement_course_1_c_0,
       twos_complement_course_1_c_1, twos_complement_course_1_c_2, twos_complement_course_1_c_3,
       twos_complement_course_1_c_4, twos_complement_course_1_c_5, twos_complement_course_1_c_6,
       twos_complement_course_1_c_7;

  not not_1 (not_1_out, i_2_bit_7);
  twos_complement_course twos_complement_course_1 (
    .s_7(not_1_out), .s_6(i_2_bit_6), .s_5(i_2_bit_5), .s_4(i_2_bit_4), .s_3(i_2_bit_3), .s_2(i_2_bit_2),
    .s_1(i_2_bit_1), .s_0(i_2_bit_0), .c_7(twos_complement_course_1_c_7), .c_6(twos_complement_course_1_c_6),
    .c_5(twos_complement_course_1_c_5), .c_4(twos_complement_course_1_c_4),
    .c_3(twos_complement_course_1_c_3), .c_2(twos_complement_course_1_c_2),
    .c_1(twos_complement_course_1_c_1), .c_0(twos_complement_course_1_c_0));
  Multiplexer multiplexer_1 (.sel(Sgn), .in_0(i_2_bit_7), .in_1(twos_complement_course_1_c_7), .out(multiplexer_1_out));
  Multiplexer multiplexer_2 (.sel(Sgn), .in_0(i_2_bit_6), .in_1(twos_complement_course_1_c_6), .out(multiplexer_2_out));
  Multiplexer multiplexer_3 (.sel(Sgn), .in_0(i_2_bit_5), .in_1(twos_complement_course_1_c_5), .out(multiplexer_3_out));
  Multiplexer multiplexer_4 (.sel(Sgn), .in_0(i_2_bit_4), .in_1(twos_complement_course_1_c_4), .out(multiplexer_4_out));
  Multiplexer multiplexer_5 (.sel(Sgn), .in_0(i_2_bit_3), .in_1(twos_complement_course_1_c_3), .out(multiplexer_5_out));
  Multiplexer multiplexer_6 (.sel(Sgn), .in_0(i_2_bit_2), .in_1(twos_complement_course_1_c_2), .out(multiplexer_6_out));
  Multiplexer multiplexer_7 (.sel(Sgn), .in_0(i_2_bit_1), .in_1(twos_complement_course_1_c_1), .out(multiplexer_7_out));
  Multiplexer multiplexer_8 (.sel(Sgn), .in_0(i_2_bit_0), .in_1(twos_complement_course_1_c_0), .out(multiplexer_8_out));
  _8bits_adder _8bits_adder_1 (
    .a_7(i_1_bit_7), .a_6(i_1_bit_6), .a_5(i_1_bit_5), .a_4(i_1_bit_4), .a_3(i_1_bit_3), .a_2(i_1_bit_2),
    .a_1(i_1_bit_1), .a_0(i_1_bit_0), .b_7(multiplexer_1_out), .b_6(multiplexer_2_out),
    .b_5(multiplexer_3_out), .b_4(multiplexer_4_out), .b_3(multiplexer_5_out), .b_2(multiplexer_6_out),
    .b_1(multiplexer_7_out), .b_0(multiplexer_8_out), .s_7(o_7), .s_6(o_6), .s_5(o_5), .s_4(o_4), .s_3(o_3),
    .s_2(o_2), .s_1(o_1), .s_0(o_0));  // open: t_7, t_6, t_5, t_4, t_3, t_2, t_1, t_0, r_1, R_1_2
endmodule
