// Digital circuit impulse-output.dig as structural Verilog
module impulse_output (
  input  Trigger,
  input  Clk,
  output ImpulseOutput,
  output ClkOutput
);

  wire d_ff_1_q, d_ff_2_nq;

  D_FF d_ff_1 (.D(Trigger), .C(Clk), .Q(d_ff_1_q));  // open: nQ
  D_FF d_ff_2 (.D(d_ff_1_q), .C(Clk), .nQ(d_ff_2_nq));  // open: Q
  and and_1 (ImpulseOutput, d_ff_1_q, d_ff_2_nq);

  assign ClkOutput = Clk;
endmodule
