// Digital circuit load+store+3+2.dig as structural Verilog
module load_store_3_2 (
  input  i_0,
  input  i_1,
  input  i_2,
  input  i_3,
  input  i_4,
  input  i_5,
  input  i_6,
  input  i_7,
  input  m_00,
  input  m_01,
  input  m_02,
  input  Clk,
  input  On_Off,
  input  m_10,
  input  m_11,
  input  m_12,
  input  m_20,
  input  m_21,
  input  m_22,
  input  lm_00,
  input  lm_01,
  input  lm_02,
  input  lm_10,
  input  lm_11,
  input  lm_12,
  input  lm_20,
  input  lm_21,
  input  lm_22,
  input  r_1,
  input  r_2,
  output o_10,
  output o_11,
  output o_12,
  output o_13,
  output o_14,
  output o_15,
  output o_16,
  output o_17,
  output o_20,
  output o_21,
  output o_22,
  output o_23,
  output o_24,
  output o_25,
  output o_26,
  output o_27
);

  wire _8_bit_memories_1_output_0, _8_bit_memories_1_output_1, _8_bit_memories_1_output_2,
       _8_bit_memories_1_output_3, _8_bit_memories_1_output_4, _8_bit_memories_1_output_5,
       _8_bit_memories_1_output_6, _8_bit_memories_1_output_7, _8_bit_memories_2_output_0,
       _8_bit_memories_2_output_1, _8_bit_memories_2_output_2, _8_bit_memories_2_output_3,
       _8_bit_memories_2_output_4, _8_bit_memories_2_output_5, _8_bit_memories_2_output_6,
       _8_bit_memories_2_output_7, _8_bit_memories_3_output_0, _8_bit_memories_3_output_1,
       _8_bit_memories_3_output_2, _8_bit_memories_3_output_3, _8_bit_memories_3_output_4,
       _8_bit_memories_3_output_5, _8_bit_memories_3_output_6, _8_bit_memories_3_output_7, and_1_out,
       and_2_out, d_ff_1_q, d_ff_2_q, d_ff_3_q, multiplexer_1_out, multiplexer_2_out, multiplexer_3_out,
       multiplexer_4_out, multiplexer_5_out, multiplexer_6_out, multiplexer_7_out, multiplexer_8_out,
       multiplexer_9_out, multiplexer_10_out, or_1_out, or_2_out, or_3_out, or_4_out, or_5_out, or_6_out,
       or_7_out, or_8_out;

  D_FF d_ff_1 (.D(On_Off), .C(Clk), .Q(d_ff_1_q));  // open: nQ
  _8_bit_memories _8_bit_memories_1 (
    .InputBit_7(i_7), .InputBit_6(i_6), .InputBit_5(i_5), .InputBit_4(i_4), .InputBit_3(i_3),
    .InputBit_2(i_2), .InputBit_1(i_1), .InputBit_0(i_0), .SelMemory_2(multiplexer_4_out),
    .SelMemory_1(multiplexer_3_out), .SelMemory_0(multiplexer_2_out), .Read_Write(multiplexer_1_out),
    .Output_7(_8_bit_memories_1_output_7), .Output_6(_8_bit_memories_1_output_6),
    .Output_5(_8_bit_memories_1_output_5), .Output_4(_8_bit_memories_1_output_4),
    .Output_3(_8_bit_memories_1_output_3), .Output_2(_8_bit_memories_1_output_2),
    .Output_1(_8_bit_memories_1_output_1), .Output_0(_8_bit_memories_1_output_0), .Enable(d_ff_1_q));
  _8_bit_memories _8_bit_memories_2 (
    .InputBit_7(i_7), .InputBit_6(i_6), .InputBit_5(i_5), .InputBit_4(i_4), .InputBit_3(i_3),
    .InputBit_2(i_2), .InputBit_1(i_1), .InputBit_0(i_0), .SelMemory_2(multiplexer_7_out),
    .SelMemory_1(multiplexer_6_out), .SelMemory_0(multiplexer_5_out), .Read_Write(multiplexer_1_out),
    .Output_7(_8_bit_memories_2_output_7), .Output_6(_8_bit_memories_2_output_6),
    .Output_5(_8_bit_memories_2_output_5), .Output_4(_8_bit_memories_2_output_4),
    .Output_3(_8_bit_memories_2_output_3), .Output_2(_8_bit_memories_2_output_2),
    .Output_1(_8_bit_memories_2_output_1), .Output_0(_8_bit_memories_2_output_0), .Enable(d_ff_1_q));
  Multiplexer multiplexer_1 (.sel(d_ff_1_q), .in_0(1'b0), .in_1(1'b1), .out(multiplexer_1_out));
  _8_bit_memories _8_bit_memories_3 (
    .InputBit_7(i_7), .InputBit_6(i_6), .InputBit_5(i_5), .InputBit_4(i_4), .InputBit_3(i_3),
    .InputBit_2(i_2), .InputBit_1(i_1), .InputBit_0(i_0), .SelMemory_2(multiplexer_10_out),
    .SelMemory_1(multiplexer_9_out), .SelMemory_0(multiplexer_8_out), .Read_Write(multiplexer_1_out),
    .Output_7(_8_bit_memories_3_output_7), .Output_6(_8_bit_memories_3_output_6),
    .Output_5(_8_bit_memories_3_output_5), .Output_4(_8_bit_memories_3_output_4),
    .Output_3(_8_bit_memories_3_output_3), .Output_2(_8_bit_memories_3_output_2),
    .Output_1(_8_bit_memories_3_output_1), .Output_0(_8_bit_memories_3_output_0), .Enable(d_ff_1_q));
  Multiplexer multiplexer_2 (.sel(d_ff_1_q), .in_0(lm_00), .in_1(m_00), .out(multiplexer_2_out));
  Multiplexer multiplexer_3 (.sel(d_ff_1_q), .in_0(lm_01), .in_1(m_01), .out(multiplexer_3_out));
  Multiplexer multiplexer_4 (.sel(d_ff_1_q), .in_0(lm_02), .in_1(m_02), .out(multiplexer_4_out));
  Multiplexer multiplexer_5 (.sel(d_ff_1_q), .in_0(lm_10), .in_1(m_10), .out(multiplexer_5_out));
  Multiplexer multiplexer_6 (.sel(d_ff_1_q), .in_0(lm_11), .in_1(m_11), .out(multiplexer_6_out));
  Multiplexer multiplexer_7 (.sel(d_ff_1_q), .in_0(lm_12), .in_1(m_12), .out(multiplexer_7_out));
  Multiplexer multiplexer_8 (.sel(d_ff_1_q), .in_0(lm_20), .in_1(m_20), .out(multiplexer_8_out));
  Multiplexer multiplexer_9 (.sel(d_ff_1_q), .in_0(lm_21), .in_1(m_21), .out(multiplexer_9_out));
  Multiplexer multiplexer_10 (.sel(d_ff_1_q), .in_0(lm_22), .in_1(m_22), .out(multiplexer_10_out));
  or or_1 (or_1_out, _8_bit_memories_3_output_7, _8_bit_memories_2_output_7, _8_bit_memories_1_output_7);
  or or_2 (or_2_out, _8_bit_memories_3_output_6, _8_bit_memories_2_output_6, _8_bit_memories_1_output_6);
  or or_3 (or_3_out, _8_bit_memories_3_output_5, _8_bit_memories_2_output_5, _8_bit_memories_1_output_5);
  or or_4 (or_4_out, _8_bit_memories_3_output_4, _8_bit_memories_2_output_4, _8_bit_memories_1_output_4);
  or or_5 (or_5_out, _8_bit_memories_3_output_3, _8_bit_memories_2_output_3, _8_bit_memories_1_output_3);
  or or_6 (or_6_out, _8_bit_memories_3_output_2, _8_bit_memories_2_output_2, _8_bit_memories_1_output_2);
  or or_7 (or_7_out, _8_bit_memories_3_output_1, _8_bit_memories_2_output_1, _8_bit_memories_1_output_1);
  or or_8 (or_8_out, _8_bit_memories_3_output_0, _8_bit_memories_2_output_0, _8_bit_memories_1_output_0);
  and and_1 (and_1_out, r_1, d_ff_1_q);
  D_FF d_ff_2 (.D(and_1_out), .C(Clk), .Q(d_ff_2_q));  // open: nQ
  and and_2 (and_2_out, r_2, d_ff_1_q);
  D_FF d_ff_3 (.D(and_2_out), .C(Clk), .Q(d_ff_3_q));  // open: nQ
  _8_bit_register _8_bit_register_1 (
    .Clk(Clk), .i_7(or_1_out), .i_6(or_2_out), .i_5(or_3_out), .i_4(or_4_out), .i_3(or_5_out),
    .i_2(or_6_out), .i_1(or_7_out), .i_0(or_8_out), .Enable(d_ff_2_q), .o_7(o_27), .o_6(o_26), .o_5(o_25),
    .o_4(o_24), .o_3(o_23), .o_2(o_22), .o_1(o_21), .o_0(o_20));
  _8_bit_register _8_bit_register_2 (
    .Clk(Clk), .i_7(or_1_out), .i_6(or_2_out), .i_5(or_3_out), .i_4(or_4_out), .i_3(or_5_out),
    .i_2(or_6_out), .i_1(or_7_out), .i_0(or_8_out), .Enable(d_ff_3_q), .o_7(o_17), .o_6(o_16), .o_5(o_15),
    .o_4(o_14), .o_3(o_13), .o_2(o_12), .o_1(o_11), .o_0(o_10));
endmodule
