// Digital circuit load.dig as structural Verilog
module load (
  input  i_0,
  input  i_1,
  input  i_2,
  input  i_3,
  input  i_4,
  input  i_5,
  input  i_6,
  input  i_7,
  input  Storem_0,
  input  Storem_1,
  input  Storem_2,
  input  Clk,
  input  Loadm_0,
  input  on_off,
  input  Loadm_1,
  input  Loadm_2,
  output o_0,
  output o_1,
  output o_2,
  output o_3,
  output o_4,
  output o_5,
  output o_6,
  output o_7
);

  wire _8_bit_memories_1_output_0, _8_bit_memories_1_output_1, _8_bit_memories_1_output_2,
       _8_bit_memories_1_output_3, _8_bit_memories_1_output_4, _8_bit_memories_1_output_5,
       _8_bit_memories_1_output_6, _8_bit_memories_1_output_7, d_ff_1_q, d_ff_2_q, multiplexer_1_out,
       multiplexer_2_out, multiplexer_3_out, multiplexer_4_out;

  Multiplexer multiplexer_1 (.sel(d_ff_2_q), .in_0(1'b0), .in_1(1'b1), .out(multiplexer_1_out));
  D_FF d_ff_1 (.D(on_off), .C(Clk), .Q(d_ff_1_q));  // open: nQ
  Multiplexer multiplexer_2 (.sel(d_ff_2_q), .in_0(Loadm_0), .in_1(Storem_0), .out(multiplexer_2_out));
  Multiplexer multiplexer_3 (.sel(d_ff_2_q), .in_0(Loadm_1), .in_1(Storem_1), .out(multiplexer_3_out));
  Multiplexer multiplexer_4 (.sel(d_ff_2_q), .in_0(Loadm_2), .in_1(Storem_2), .out(multiplexer_4_out));
  _8_bit_memories _8_bit_memories_1 (
    .Clk(d_ff_1_q), .InputBit_7(i_7), .InputBit_6(i_6), .InputBit_5(i_5), .InputBit_4(i_4), .InputBit_3(i_3),
    .InputBit_2(i_2), .InputBit_1(i_1), .InputBit_0(i_0), .SelMemory_2(multiplexer_4_out),
    .SelMemory_1(multiplexer_3_out), .SelMemory_0(multiplexer_2_out), .Read_Write(multiplexer_1_out),
    .Output_7(_8_bit_memories_1_output_7), .Output_6(_8_bit_memories_1_output_6),
    .Output_5(_8_bit_memories_1_output_5), .Output_4(_8_bit_memories_1_output_4),
    .Output_3(_8_bit_memories_1_output_3), .Output_2(_8_bit_memories_1_output_2),
    .Output_1(_8_bit_memories_1_output_1), .Output_0(_8_bit_memories_1_output_0));
  D_FF d_ff_2 (.D(d_ff_1_q), .C(Clk), .Q(d_ff_2_q));  // open: nQ
  _8_bit_register _8_bit_register_1 (
    .Clk(Clk), .i_7(_8_bit_memories_1_output_7), .i_6(_8_bit_memories_1_output_6),
    .i_5(_8_bit_memories_1_output_5), .i_4(_8_bit_memories_1_output_4), .i_3(_8_bit_memories_1_output_3),
    .i_2(_8_bit_memories_1_output_2), .i_1(_8_bit_memories_1_output_1), .i_0(_8_bit_memories_1_output_0),
    .Enable(d_ff_2_q), .o_7(o_7), .o_6(o_6), .o_5(o_5), .o_4(o_4), .o_3(o_3), .o_2(o_2), .o_1(o_1), .o_0(o_0));

  // Notes on the sheet:
  //   Store Instruction
  //   Load Instruction
endmodule
