// Digital circuit store.dig as structural Verilog
module store (
  input  i_0,
  input  i_1,
  input  i_2,
  input  i_3,
  input  i_4,
  input  i_5,
  input  i_6,
  input  i_7,
  input  m_00,
  input  m_01,
  input  m_02,
  input  Clk,
  input  On_Off,
  input  m_10,
  input  m_11,
  input  m_12,
  input  m_20,
  input  m_21,
  input  m_22
);

  wire _8_bit_memories_1_output_0, _8_bit_memories_1_output_1, _8_bit_memories_1_output_2,
       _8_bit_memories_1_output_3, _8_bit_memories_1_output_4, _8_bit_memories_1_output_5,
       _8_bit_memories_1_output_6, _8_bit_memories_1_output_7, _8_bit_memories_2_output_0,
       _8_bit_memories_2_output_1, _8_bit_memories_2_output_2, _8_bit_memories_2_output_3,
       _8_bit_memories_2_output_4, _8_bit_memories_2_output_5, _8_bit_memories_2_output_6,
       _8_bit_memories_2_output_7, _8_bit_memories_3_output_0, _8_bit_memories_3_output_1,
       _8_bit_memories_3_output_2, _8_bit_memories_3_output_3, _8_bit_memories_3_output_4,
       _8_bit_memories_3_output_5, _8_bit_memories_3_output_6, _8_bit_memories_3_output_7, and_1_out,
       d_ff_1_q, or_1_out, or_2_out, or_3_out, or_4_out, or_5_out, or_6_out, or_7_out, or_8_out;

  D_FF d_ff_1 (.D(On_Off), .C(Clk), .Q(d_ff_1_q));  // open: nQ
  and and_1 (and_1_out, d_ff_1_q, Clk);
  _8_bit_memories _8_bit_memories_1 (
    .Clk(and_1_out), .InputBit_7(i_7), .InputBit_6(i_6), .InputBit_5(i_5), .InputBit_4(i_4),
    .InputBit_3(i_3), .InputBit_2(i_2), .InputBit_1(i_1), .InputBit_0(i_0), .SelMemory_2(m_02),
    .SelMemory_1(m_01), .SelMemory_0(m_00), .Read_Write(1'b1), .Output_7(_8_bit_memories_1_output_7),
    .Output_6(_8_bit_memories_1_output_6), .Output_5(_8_bit_memories_1_output_5),
    .Output_4(_8_bit_memories_1_output_4), .Output_3(_8_bit_memories_1_output_3),
    .Output_2(_8_bit_memories_1_output_2), .Output_1(_8_bit_memories_1_output_1),
    .Output_0(_8_bit_memories_1_output_0));
  _8_bit_memories _8_bit_memories_2 (
    .Clk(and_1_out), .InputBit_7(i_7), .InputBit_6(i_6), .InputBit_5(i_5), .InputBit_4(i_4),
    .InputBit_3(i_3), .InputBit_2(i_2), .InputBit_1(i_1), .InputBit_0(i_0), .SelMemory_2(m_12),
    .SelMemory_1(m_11), .SelMemory_0(m_10), .Read_Write(1'b1), .Output_7(_8_bit_memories_2_output_7),
    .Output_6(_8_bit_memories_2_output_6), .Output_5(_8_bit_memories_2_output_5),
    .Output_4(_8_bit_memories_2_output_4), .Output_3(_8_bit_memories_2_output_3),
    .Output_2(_8_bit_memories_2_output_2), .Output_1(_8_bit_memories_2_output_1),
    .Output_0(_8_bit_memories_2_output_0));
  or or_1 (or_1_out, _8_bit_memories_1_output_7, _8_bit_memories_2_output_7, _8_bit_memories_3_output_7);
  or or_2 (or_2_out, _8_bit_memories_3_output_6, _8_bit_memories_2_output_6, _8_bit_memories_1_output_6);
  or or_3 (or_3_out, _8_bit_memories_3_output_5, _8_bit_memories_2_output_5, _8_bit_memories_1_output_5);
  or or_4 (or_4_out, _8_bit_memories_3_output_4, _8_bit_memories_2_output_4, _8_bit_memories_1_output_4);
  or or_5 (or_5_out, _8_bit_memories_3_output_3, _8_bit_memories_2_output_3, _8_bit_memories_1_output_3);
  or or_6 (or_6_out, _8_bit_memories_3_output_2, _8_bit_memories_2_output_2, _8_bit_memories_1_output_2);
  or or_7 (or_7_out, _8_bit_memories_3_output_1, _8_bit_memories_2_output_1, _8_bit_memories_1_output_1);
  or or_8 (or_8_out, _8_bit_memories_3_output_0, _8_bit_memories_2_output_0, _8_bit_memories_1_output_0);
  _8_bit_memories _8_bit_memories_3 (
    .Clk(and_1_out), .InputBit_7(i_7), .InputBit_6(i_6), .InputBit_5(i_5), .InputBit_4(i_4),
    .InputBit_3(i_3), .InputBit_2(i_2), .InputBit_1(i_1), .InputBit_0(i_0), .SelMemory_2(m_22),
    .SelMemory_1(m_21), .SelMemory_0(m_20), .Read_Write(1'b1), .Output_7(_8_bit_memories_3_output_7),
    .Output_6(_8_bit_memories_3_output_6), .Output_5(_8_bit_memories_3_output_5),
    .Output_4(_8_bit_memories_3_output_4), .Output_3(_8_bit_memories_3_output_3),
    .Output_2(_8_bit_memories_3_output_2), .Output_1(_8_bit_memories_3_output_1),
    .Output_0(_8_bit_memories_3_output_0));
  LED ClkOutput (.in(Clk));
  LED o_7 (.in(or_1_out));
  LED o_6 (.in(or_2_out));
  LED o_5 (.in(or_3_out));
  LED o_4 (.in(or_4_out));
  LED o_3 (.in(or_5_out));
  LED o_2 (.in(or_6_out));
  LED o_1 (.in(or_7_out));
  LED o_0 (.in(or_8_out));

  // Notes on the sheet:
  //   Input
endmodule
