// Digital circuit store_1bit.dig as structural Verilog
module store_1bit (
  input  On_Off,
  input  Clk,
  input  i_0,
  input  i_1,
  input  i_2,
  input  i_3,
  input  i_4,
  input  i_5,
  input  i_6,
  input  i_7,
  input  m_2,
  input  m_1,
  input  m_0,
  output o_0,
  output o_1,
  output o_2,
  output o_3,
  output o_4,
  output o_5,
  output o_6,
  output o_7,
  output o_clk
);

  wire and_1_out, d_ff_1_q;

  D_FF d_ff_1 (.D(On_Off), .C(Clk), .Q(d_ff_1_q));  // open: nQ
  and and_1 (and_1_out, d_ff_1_q, Clk);
  _8_bit_memories _8_bit_memories_1 (
    .Clk(and_1_out), .InputBit_7(i_7), .InputBit_6(i_6), .InputBit_5(i_5), .InputBit_4(i_4),
    .InputBit_3(i_3), .InputBit_2(i_2), .InputBit_1(i_1), .InputBit_0(i_0), .SelMemory_2(m_2),
    .SelMemory_1(m_1), .SelMemory_0(m_0), .Read_Write(1'b1), .Output_7(o_7), .Output_6(o_6), .Output_5(o_5),
    .Output_4(o_4), .Output_3(o_3), .Output_2(o_2), .Output_1(o_1), .Output_0(o_0));

  assign o_clk = Clk;
endmodule
