// Digital circuit test.dig as structural Verilog
module test (
  input  s_0,
  input  s_1,
  input  s_2,
  input  s_3,
  input  s_4,
  input  s_5,
  input  s_6,
  input  Signe1,
  input  Clk,
  input  Claculer,
  input  s_8,
  input  s_9,
  input  s_10,
  input  s_11,
  input  s_12,
  input  s_13,
  input  s_14,
  input  Signe2,
  output M_0,
  output M_1,
  output M_2,
  output M_3,
  output M_4,
  output M_5,
  output M_6,
  output M_7
);

  wire \asyn_1_durée , \asyn_2_durée , \asyn_3_durée , \asyn_4_durée , \asyn_5_durée , d_ff_1_q, d_ff_2_q,
       d_ff_3_q, d_ff_4_q, d_ff_5_q, d_ff_6_q, store_1_p10, store_1_p11, store_1_p12, store_1_p13,
       store_1_p14, store_1_p15, store_1_p16, store_1_p17, store_1_p18, store_1_p28, store_1_p29,
       store_1_p30, store_1_p31, store_1_p32, store_1_p33, store_1_p34, store_1_p35, store_1_p43,
       store_1_p44, store_1_p45, store_1_p46, store_2_p10, store_2_p11, store_2_p12, store_2_p13,
       store_2_p14, store_2_p15, store_2_p16, store_2_p17, store_2_p18, store_2_p28, store_2_p29,
       store_2_p30, store_2_p31, store_2_p32, store_2_p33, store_2_p34, store_2_p35, store_3_p1, store_3_p2,
       store_3_p5, store_3_p6, store_3_p7, store_3_p8, store_3_p9, store_3_p10, store_3_p12, store_3_p13,
       store_3_p14, store_3_p15, store_3_p16, store_3_p17, store_3_p18, store_3_p19, store_3_p20;

  D_FF d_ff_1 (.D(Claculer), .C(Clk), .Q(d_ff_1_q));  // open: nQ
  D_FF d_ff_2 (.D(d_ff_1_q), .C(Clk), .Q(d_ff_2_q));  // open: nQ
  Asyn asyn_1 (.Com(d_ff_1_q), .Arr(d_ff_2_q), .\Durée (\asyn_1_durée ));
  // STORE store_1: pin names not known; wires that end beside it: Signe1, s_6, s_5, s_4, s_3, s_2, s_1, s_0, \asyn_1_durée , store_1_p10, store_1_p11, store_1_p12, store_1_p13, store_1_p14, store_1_p15, store_1_p16, store_1_p17, store_1_p18, store_1_p10, store_1_p11, store_1_p12, store_1_p13, store_1_p14, store_1_p15, store_1_p16, store_1_p17, Clk, store_1_p28, store_1_p29, store_1_p30, store_1_p31, store_1_p32, store_1_p33, store_1_p34, store_1_p35, store_1_p18, store_1_p28, store_1_p29, store_1_p30, store_1_p31, store_1_p32, store_1_p33, store_1_p43, store_1_p44, store_1_p45, store_1_p46
  // STORE store_2: pin names not known; wires that end beside it: Signe2, s_14, s_13, s_12, s_11, s_10, s_9, s_8, \asyn_1_durée , store_2_p10, store_2_p11, store_2_p12, store_2_p13, store_2_p14, store_2_p15, store_2_p16, store_2_p17, store_2_p18, store_2_p10, store_2_p11, store_2_p12, store_2_p13, store_2_p14, store_2_p15, store_2_p16, store_2_p17, Clk, store_2_p28, store_2_p29, store_2_p30, store_2_p31, store_2_p32, store_2_p33, store_2_p34, store_2_p35, store_2_p18
  Memoire memoire_1 ();
  D_FF d_ff_3 (.D(d_ff_2_q), .C(Clk), .Q(d_ff_3_q));  // open: nQ
  Memoire memoire_2 ();
  LOAD load_1 ();
  Asyn asyn_2 (.Com(d_ff_2_q), .Arr(d_ff_6_q), .\Durée (\asyn_2_durée ));
  D_FF d_ff_4 (.D(d_ff_3_q), .C(Clk), .Q(d_ff_4_q));  // open: nQ
  LOAD load_2 ();
  Asyn asyn_3 (.Com(d_ff_3_q), .Arr(d_ff_6_q), .\Durée (\asyn_3_durée ));
  ALU alu_1 ();
  D_FF d_ff_5 (.D(d_ff_4_q), .C(Clk), .Q(d_ff_5_q));  // open: nQ
  Asyn asyn_4 (.Com(d_ff_4_q), .Arr(d_ff_6_q), .\Durée (\asyn_4_durée ));
  Asyn asyn_5 (.Com(d_ff_5_q), .Arr(d_ff_6_q), .\Durée (\asyn_5_durée ));
  D_FF d_ff_6 (.D(d_ff_5_q), .C(Clk), .Q(d_ff_6_q));  // open: nQ
  // STORE store_3: pin names not known; wires that end beside it: store_3_p1, store_3_p2, store_3_p1, store_3_p2, store_3_p5, store_3_p6, store_3_p7, store_3_p8, store_3_p9, store_3_p10, \asyn_5_durée , store_3_p12, store_3_p13, store_3_p14, store_3_p15, store_3_p16, store_3_p17, store_3_p18, store_3_p19, store_3_p20, store_3_p12, store_3_p13, store_3_p14, store_3_p15, store_3_p16, store_3_p17, store_3_p18, store_3_p19, Clk, M_7, M_6, M_5, M_4, M_3, M_2, M_1, M_0
  Memoire memoire_3 ();

  // Notes on the sheet:
  //   Clk: Hz: 200
endmodule
