// Digital circuit Register.dig as structural Verilog
module Register (
  input  Input,
  input  Enable_Pin,
  input  Clock,
  output Output
);

  Register register_1 (.D(Input), .C(Clock), .en(Enable_Pin), .Q(Output));
endmodule
