// Digital circuit Complément_8bit.dig as structural Verilog
module \Complément_8bit  (
  input  a_1,
  input  a_2,
  input  a_3,
  input  a_4,
  input  a_5,
  input  a_6,
  input  a_7,
  input  a_8,
  output c_1,
  output c_2,
  output c_3,
  output c_4,
  output c_5,
  output c_6,
  output c_7,
  output c_8
);

  wire c_1bit_1_s_1, c_1bit_2_s_1, c_1bit_3_s_1, c_1bit_4_s_1, c_1bit_5_s_1, c_1bit_6_s_1, c_1bit_7_s_1,
       xor_1_out, xor_2_out, xor_3_out, xor_4_out, xor_5_out, xor_6_out, xor_7_out;

  LED led_1 (.in(a_8));
  LED led_2 (.in(a_7));
  LED led_3 (.in(a_6));
  LED led_4 (.in(a_5));
  LED led_5 (.in(a_4));
  LED led_6 (.in(a_3));
  LED led_7 (.in(a_2));
  LED led_8 (.in(a_1));
  LED led_9 (.in(c_8));
  LED led_10 (.in(c_7));
  LED led_11 (.in(c_6));
  LED led_12 (.in(c_5));
  LED led_13 (.in(c_4));
  LED led_14 (.in(c_3));
  LED led_15 (.in(c_2));
  LED led_16 (.in(c_1));
  xor xor_1 (xor_1_out, a_8, a_1);
  c_1bit c_1bit_1 (.p_1(a_8), .p_0(xor_1_out), .s_1(c_1bit_1_s_1), .s_0(c_1));
  xor xor_2 (xor_2_out, a_8, a_2);
  c_1bit c_1bit_2 (.p_1(c_1bit_1_s_1), .p_0(xor_2_out), .s_1(c_1bit_2_s_1), .s_0(c_2));
  xor xor_3 (xor_3_out, a_8, a_3);
  c_1bit c_1bit_3 (.p_1(c_1bit_2_s_1), .p_0(xor_3_out), .s_1(c_1bit_3_s_1), .s_0(c_3));
  xor xor_4 (xor_4_out, a_8, a_4);
  c_1bit c_1bit_4 (.p_1(c_1bit_3_s_1), .p_0(xor_4_out), .s_1(c_1bit_4_s_1), .s_0(c_4));
  xor xor_5 (xor_5_out, a_8, a_5);
  c_1bit c_1bit_5 (.p_1(c_1bit_4_s_1), .p_0(xor_5_out), .s_1(c_1bit_5_s_1), .s_0(c_5));
  xor xor_6 (xor_6_out, a_8, a_6);
  c_1bit c_1bit_6 (.p_1(c_1bit_5_s_1), .p_0(xor_6_out), .s_1(c_1bit_6_s_1), .s_0(c_6));
  xor xor_7 (xor_7_out, a_8, a_7);
  c_1bit c_1bit_7 (.p_1(c_1bit_6_s_1), .p_0(xor_7_out), .s_1(c_1bit_7_s_1), .s_0(c_7));
  xor xor_8 (c_8, a_8, c_1bit_7_s_1);
endmodule
