// Digital circuit 2's_complement_8bit.dig as structural Verilog
module _2_s_complement_8bit (
  input  in_1,
  input  in_2,
  input  in_3,
  input  in_4,
  output out_5,
  output out_6,
  output out_7,
  output out_8
);

  wire _2_s_complement_adder_1bit_1_carryout, _2_s_complement_adder_1bit_2_carryout;

  _2_s_complement_adder_1bit _2_s_complement_adder_1bit_1 (
    .CarryIn(1'b0), .b(in_4), .bInvertSel(in_1), .CarryOut(_2_s_complement_adder_1bit_1_carryout),
    .AddResult(out_5));
  _2_s_complement_adder_1bit _2_s_complement_adder_1bit_2 (
    .CarryIn(_2_s_complement_adder_1bit_1_carryout), .b(in_3), .bInvertSel(in_1),
    .CarryOut(_2_s_complement_adder_1bit_2_carryout), .AddResult(out_6));
  _2_s_complement_adder_1bit _2_s_complement_adder_1bit_3 (
    .CarryIn(_2_s_complement_adder_1bit_2_carryout), .b(in_2), .bInvertSel(in_1), .AddResult(out_7));  // open: CarryOut

  assign out_8 = in_1;
endmodule
