// Digital circuit 2's_complement_adder_1bit.dig as structural Verilog
module _2_s_complement_adder_1bit (
  input  b,
  input  CarryIn,
  input  bInvertSel,
  output CarryOut,
  output AddResult
);

  wire multiplexer_1_out, not_1_out;

  not not_1 (not_1_out, b);
  Multiplexer multiplexer_1 (.sel(bInvertSel), .in_0(b), .in_1(not_1_out), .out(multiplexer_1_out));
  alu_1bit alu_1bit_1 (
    .a(1'b0), .b(multiplexer_1_out), .AddResult(AddResult), .CarryOut(CarryOut), .CarryIn(CarryIn));  // open: AndResult, OrResult
endmodule
