// Digital circuit adder_calculate_carry_out_1bit.dig as structural Verilog
module adder_calculate_carry_out_1bit (
  input  a,
  input  CarryIn,
  input  b,
  output CarryOut
);

  wire and_1_out, and_2_out, and_3_out, or_1_out;

  and and_1 (and_1_out, a, CarryIn);
  and and_2 (and_2_out, CarryIn, b);
  and and_3 (and_3_out, a, b);
  or or_1 (or_1_out, and_1_out, and_2_out);
  or or_2 (CarryOut, or_1_out, and_3_out);
endmodule
