// Digital circuit alu_1bit.dig as structural Verilog
module alu_1bit (
  input  a,
  input  b,
  input  CarryIn,
  output AndResult,
  output OrResult,
  output AddResult,
  output CarryOut
);

  and and_1 (AndResult, a, b);
  or or_1 (OrResult, a, b);
  adder_1bit adder_1bit_1 (.a(a), .b(b), .CarryIn(CarryIn), .Result(AddResult), .CarryOut(CarryOut));
endmodule
