// Digital circuit and_or_selection_unit.dig as structural Verilog
module and_or_selection_unit (
  input  a,
  input  b,
  input  selection,
  output result
);

  wire and_1_out, or_1_out;

  and and_1 (and_1_out, a, b);
  or or_1 (or_1_out, a, b);
  Multiplexer multiplexer_1 (.sel(selection), .in_0(and_1_out), .in_1(or_1_out), .out(result));
endmodule
