// Digital circuit Compl谷ment_8bit_DPR.dig as structural Verilog
module \Compl谷ment_8bit_DPR  (
  input  a_1,
  input  a_2,
  input  a_3,
  input  a_4,
  input  a_5,
  input  a_6,
  input  a_7,
  input  a_8,
  output s_1,
  output s_2,
  output s_3,
  output s_4,
  output s_5,
  output s_6,
  output s_7,
  output s_8
);

  wire multiplexer_1_out, multiplexer_2_out, multiplexer_3_out, multiplexer_4_out, multiplexer_5_out,
       multiplexer_6_out, multiplexer_7_out, not_1_out, not_2_out, not_3_out, not_4_out, not_5_out,
       not_6_out, not_7_out;

  Multiplexer multiplexer_1 (.sel(a_8), .in_0(a_7), .in_1(not_1_out), .out(multiplexer_1_out));
  not not_1 (not_1_out, a_7);
  Multiplexer multiplexer_2 (.sel(a_8), .in_0(a_6), .in_1(not_2_out), .out(multiplexer_2_out));
  not not_2 (not_2_out, a_6);
  Multiplexer multiplexer_3 (.sel(a_8), .in_0(a_5), .in_1(not_3_out), .out(multiplexer_3_out));
  not not_3 (not_3_out, a_5);
  Multiplexer multiplexer_4 (.sel(a_8), .in_0(a_4), .in_1(not_4_out), .out(multiplexer_4_out));
  not not_4 (not_4_out, a_4);
  Multiplexer multiplexer_5 (.sel(a_8), .in_0(a_3), .in_1(not_5_out), .out(multiplexer_5_out));
  not not_5 (not_5_out, a_3);
  Multiplexer multiplexer_6 (.sel(a_8), .in_0(a_2), .in_1(not_6_out), .out(multiplexer_6_out));
  not not_6 (not_6_out, a_2);
  Multiplexer multiplexer_7 (.sel(a_8), .in_0(a_1), .in_1(not_7_out), .out(multiplexer_7_out));
  not not_7 (not_7_out, a_1);
  _8_bitADD _8_bitadd_1 (
    .a_7(multiplexer_1_out), .a_6(multiplexer_2_out), .a_5(multiplexer_3_out), .a_4(multiplexer_4_out),
    .a_3(multiplexer_5_out), .a_2(multiplexer_6_out), .a_1(multiplexer_7_out), .a_8(1'b0), .signe(a_8),
    .s_1(s_1), .s_2(s_2), .s_3(s_3), .s_4(s_4), .s_5(s_5), .s_6(s_6), .s_7(s_7));  // open: s_8, t_1, r_1, t_2, t_3, t_4, t_5, t_6, t_7, t_8, R_1_2
  LED led_1 (.in(a_8));
  LED led_2 (.in(s_7));
  LED led_3 (.in(s_6));
  LED led_4 (.in(s_5));
  LED led_5 (.in(s_4));
  LED led_6 (.in(s_3));
  LED led_7 (.in(s_2));
  LED led_8 (.in(s_1));

  assign s_8 = a_8;
endmodule
