// Digital circuit 1-bitADD.dig as structural Verilog
module _1_bitADD (
  input  a_1,
  input  signe,
  output s_1,
  output t_1,
  output r_1,
  output R1
);

  xor xor_1 (s_1, a_1, signe);
  and and_1 (r_1, signe, a_1);
  or or_1 (R1, signe, a_1);
  not not_1 (t_1, s_1);
endmodule
