// Digital circuit 8-bitADD.dig as structural Verilog
module _8_bitADD (
  input  a_7,
  input  a_6,
  input  a_5,
  input  a_4,
  input  a_3,
  input  a_2,
  input  a_1,
  input  a_8,
  input  signe,
  output s_1,
  output s_2,
  output s_3,
  output s_4,
  output s_5,
  output s_6,
  output s_7,
  output s_8,
  output t_1,
  output r_1,
  output t_2,
  output t_3,
  output t_4,
  output t_5,
  output t_6,
  output t_7,
  output t_8,
  output R_1_2
);

  wire _4_bitadd_1_r_1, _4_bitadd_1_r_1_2, _4_bitadd_1_s_1, _4_bitadd_1_s_2, _4_bitadd_1_s_3,
       _4_bitadd_1_s_4, _4_bitadd_1_t_1, _4_bitadd_1_t_2, _4_bitadd_1_t_3, _4_bitadd_1_t_4, _4_bitadd_2_r_1,
       _4_bitadd_2_r_1_2, and_1_out, and_2_out, not_1_out, not_2_out;

  _4_bitADD _4_bitadd_1 (
    .a_4(a_8), .a_3(a_7), .a_2(a_6), .a_1(a_5), .signe(1'b0), .s_1(_4_bitadd_1_s_1), .s_2(_4_bitadd_1_s_2),
    .s_3(_4_bitadd_1_s_3), .s_4(_4_bitadd_1_s_4), .t_1(_4_bitadd_1_t_1), .t_2(_4_bitadd_1_t_2),
    .t_3(_4_bitadd_1_t_3), .t_4(_4_bitadd_1_t_4), .r_1(_4_bitadd_1_r_1), .R_1_2(_4_bitadd_1_r_1_2));
  _4_bitADD _4_bitadd_2 (
    .a_4(a_4), .a_3(a_3), .a_2(a_2), .a_1(a_1), .signe(signe), .s_1(s_1), .s_2(s_2), .s_3(s_3), .s_4(s_4),
    .t_1(t_1), .t_2(t_2), .t_3(t_3), .t_4(t_4), .r_1(_4_bitadd_2_r_1), .R_1_2(_4_bitadd_2_r_1_2));
  and and_1 (and_1_out, _4_bitadd_2_r_1, _4_bitadd_1_r_1_2);
  and and_2 (and_2_out, _4_bitadd_1_r_1_2, _4_bitadd_2_r_1_2);
  not not_1 (not_1_out, _4_bitadd_2_r_1);
  not not_2 (not_2_out, _4_bitadd_2_r_1_2);
  or or_1 (r_1, _4_bitadd_1_r_1, and_1_out);
  or or_2 (R_1_2, _4_bitadd_1_r_1, and_2_out);
  Multi_simp multi_simp_1 (
    .s_2(_4_bitadd_1_s_1), .t_2(_4_bitadd_1_t_1), .Nr(not_1_out), .r(_4_bitadd_2_r_1), .out(s_5));
  Multi_simp multi_simp_2 (
    .s_2(_4_bitadd_1_s_2), .t_2(_4_bitadd_1_t_2), .Nr(not_1_out), .r(_4_bitadd_2_r_1), .out(s_6));
  Multi_simp multi_simp_3 (
    .s_2(_4_bitadd_1_s_3), .t_2(_4_bitadd_1_t_3), .Nr(not_1_out), .r(_4_bitadd_2_r_1), .out(s_7));
  Multi_simp multi_simp_4 (
    .s_2(_4_bitadd_1_s_4), .t_2(_4_bitadd_1_t_4), .Nr(not_1_out), .r(_4_bitadd_2_r_1), .out(s_8));
  Multi_simp multi_simp_5 (
    .s_2(_4_bitadd_1_s_1), .t_2(_4_bitadd_1_t_1), .Nr(not_2_out), .r(_4_bitadd_2_r_1_2), .out(t_5));
  Multi_simp multi_simp_6 (
    .s_2(_4_bitadd_1_s_2), .t_2(_4_bitadd_1_t_2), .Nr(not_2_out), .r(_4_bitadd_2_r_1_2), .out(t_6));
  Multi_simp multi_simp_7 (
    .s_2(_4_bitadd_1_s_3), .t_2(_4_bitadd_1_t_3), .Nr(not_2_out), .r(_4_bitadd_2_r_1_2), .out(t_7));
  Multi_simp multi_simp_8 (
    .s_2(_4_bitadd_1_s_4), .t_2(_4_bitadd_1_t_4), .Nr(not_2_out), .r(_4_bitadd_2_r_1_2), .out(t_8));
  LED led_1 (.in(r_1));
  LED led_2 (.in(s_8));
  LED led_3 (.in(s_7));
  LED led_4 (.in(s_6));
  LED led_5 (.in(s_5));
  LED led_6 (.in(s_4));
  LED led_7 (.in(s_3));
  LED led_8 (.in(s_2));
  LED led_9 (.in(s_1));
endmodule
