// Digital circuit ALU.dig as structural Verilog
module ALU (
  input  R_7,
  input  R_6,
  input  R_5,
  input  R_4,
  input  R_3,
  input  R_2,
  input  R_1,
  input  R_0,
  input  R_15,
  input  R_14,
  input  R_13,
  input  R_12,
  input  R_11,
  input  R_10,
  input  R_9,
  input  R_8,
  input  Cal,
  output S_0,
  output S_1,
  output S_2,
  output S_3,
  output S_4,
  output S_5,
  output S_6,
  output S_7
);

  wire and_1_out, and_2_out, and_3_out, and_4_out, and_5_out, and_6_out, and_7_out, and_8_out, and_9_out,
       and_10_out, and_11_out, and_12_out, and_13_out, and_14_out, and_15_out, and_16_out;

  and and_1 (and_1_out, Cal, R_7);
  and and_2 (and_2_out, Cal, R_6);
  and and_3 (and_3_out, Cal, R_5);
  and and_4 (and_4_out, Cal, R_4);
  and and_5 (and_5_out, Cal, R_3);
  and and_6 (and_6_out, Cal, R_2);
  and and_7 (and_7_out, Cal, R_1);
  and and_8 (and_8_out, Cal, R_0);
  and and_9 (and_9_out, Cal, R_15);
  and and_10 (and_10_out, Cal, R_14);
  and and_11 (and_11_out, Cal, R_13);
  and and_12 (and_12_out, Cal, R_12);
  and and_13 (and_13_out, Cal, R_11);
  and and_14 (and_14_out, Cal, R_10);
  and and_15 (and_15_out, Cal, R_9);
  and and_16 (and_16_out, Cal, R_8);
  Complement_8bit_DPR complement_8bit_dpr_1 ();
  Complement_8bit_DPR complement_8bit_dpr_2 ();
  Add8bit add8bit_1 ();
endmodule
