// Digital circuit Add1bit.dig as structural Verilog
module Add1bit (
  input  a_1,
  input  b_1,
  output s_1,
  output t_1,
  output r_1,
  output R1
);

  xor xor_1 (s_1, a_1, b_1);
  and and_1 (r_1, b_1, a_1);
  or or_1 (R1, b_1, a_1);
  not not_1 (t_1, s_1);
endmodule
