// Digital circuit Complement_8bit_DPR.dig as structural Verilog
module Complement_8bit_DPR (
  input  R_7,
  input  R_6,
  input  R_5,
  input  R_4,
  input  R_3,
  input  R_2,
  input  R_1,
  input  R_0,
  output s_1,
  output s_2,
  output s_3,
  output s_4,
  output s_5,
  output s_6,
  output s_7,
  output s_8
);

  wire multiplexer_1_out, multiplexer_2_out, multiplexer_3_out, multiplexer_4_out, multiplexer_5_out,
       multiplexer_6_out, multiplexer_7_out, not_1_out, not_2_out, not_3_out, not_4_out, not_5_out,
       not_6_out, not_7_out;

  Multiplexer multiplexer_1 (.sel(R_7), .in_0(R_6), .in_1(not_1_out), .out(multiplexer_1_out));
  not not_1 (not_1_out, R_6);
  Multiplexer multiplexer_2 (.sel(R_7), .in_0(R_5), .in_1(not_2_out), .out(multiplexer_2_out));
  not not_2 (not_2_out, R_5);
  Multiplexer multiplexer_3 (.sel(R_7), .in_0(R_4), .in_1(not_3_out), .out(multiplexer_3_out));
  not not_3 (not_3_out, R_4);
  Multiplexer multiplexer_4 (.sel(R_7), .in_0(R_3), .in_1(not_4_out), .out(multiplexer_4_out));
  not not_4 (not_4_out, R_3);
  Multiplexer multiplexer_5 (.sel(R_7), .in_0(R_2), .in_1(not_5_out), .out(multiplexer_5_out));
  not not_5 (not_5_out, R_2);
  Multiplexer multiplexer_6 (.sel(R_7), .in_0(R_1), .in_1(not_6_out), .out(multiplexer_6_out));
  not not_6 (not_6_out, R_1);
  Multiplexer multiplexer_7 (.sel(R_7), .in_0(R_0), .in_1(not_7_out), .out(multiplexer_7_out));
  not not_7 (not_7_out, R_0);
  _8_bitADD _8_bitadd_1 (
    .a_7(multiplexer_1_out), .a_6(multiplexer_2_out), .a_5(multiplexer_3_out), .a_4(multiplexer_4_out),
    .a_3(multiplexer_5_out), .a_2(multiplexer_6_out), .a_1(multiplexer_7_out), .a_8(1'b0), .signe(R_7),
    .s_1(s_1), .s_2(s_2), .s_3(s_3), .s_4(s_4), .s_5(s_5), .s_6(s_6), .s_7(s_7));  // open: s_8, t_1, r_1, t_2, t_3, t_4, t_5, t_6, t_7, t_8, R_1_2
  LED led_1 (.in(R_7));
  LED led_2 (.in(s_7));
  LED led_3 (.in(s_6));
  LED led_4 (.in(s_5));
  LED led_5 (.in(s_4));
  LED led_6 (.in(s_3));
  LED led_7 (.in(s_2));
  LED led_8 (.in(s_1));

  assign s_8 = R_7;
endmodule
