// Digital circuit LOAD.dig as structural Verilog
module LOAD (
  input  M_7,
  input  M_6,
  input  M_5,
  input  M_4,
  input  M_3,
  input  M_2,
  input  M_1,
  input  M_0,
  input  LOAD,
  input  Clk,
  output R_0,
  output R_1,
  output R_2,
  output R_3,
  output R_4,
  output R_5,
  output R_6,
  output R_7
);

  wire and_1_out, and_2_out, and_3_out, and_4_out, and_5_out, and_6_out, and_7_out, and_8_out;

  and and_1 (and_1_out, LOAD, M_7);
  and and_2 (and_2_out, LOAD, M_6);
  and and_3 (and_3_out, LOAD, M_5);
  and and_4 (and_4_out, LOAD, M_4);
  and and_5 (and_5_out, LOAD, M_3);
  and and_6 (and_6_out, LOAD, M_2);
  and and_7 (and_7_out, LOAD, M_1);
  and and_8 (and_8_out, LOAD, M_0);
  Register register_1 (.D(and_1_out), .C(Clk), .en(Clk), .Q(R_7));
  Register register_2 (.D(and_2_out), .C(Clk), .en(Clk), .Q(R_6));
  Register register_3 (.D(and_3_out), .C(Clk), .en(Clk), .Q(R_5));
  Register register_4 (.D(and_4_out), .C(Clk), .en(Clk), .Q(R_4));
  Register register_5 (.D(and_5_out), .C(Clk), .en(Clk), .Q(R_3));
  Register register_6 (.D(and_6_out), .C(Clk), .en(Clk), .Q(R_2));
  Register register_7 (.D(and_7_out), .C(Clk), .en(Clk), .Q(R_1));
  Register register_8 (.D(and_8_out), .C(Clk), .en(Clk), .Q(R_0));
endmodule
