// Digital circuit Memoire-1bit.dig as structural Verilog
module Memoire_1bit (
  input  D,
  input  Clk,
  output M
);

  wire d_ff_1_nq, d_ff_1_q, d_ff_2_nq, not_1_out;

  not not_1 (not_1_out, Clk);
  D_FF d_ff_1 (.D(D), .C(Clk), .Q(d_ff_1_q), .nQ(d_ff_1_nq));
  LED led_1 (.in(d_ff_1_nq));
  D_FF d_ff_2 (.D(d_ff_1_q), .C(not_1_out), .Q(M), .nQ(d_ff_2_nq));
  LED led_2 (.in(d_ff_2_nq));
endmodule
