// Digital circuit 2bits_adder.dig as structural Verilog
module _2bits_adder (
  input  a_0,
  input  a_1,
  input  b_0,
  input  b_1,
  output s_1,
  output s_0,
  output t_1,
  output t_0,
  output r_1,
  output R_1_2
);

  wire _1bit_adder_1_r_1, _1bit_adder_1_r_1_2, _1bit_adder_1_s_1, _1bit_adder_1_t_1, _1bit_adder_2_r_1,
       _1bit_adder_2_r_1_2, and_1_out, and_2_out, and_3_out, and_4_out, and_5_out, and_6_out, not_1_out,
       not_2_out;

  _1bit_adder _1bit_adder_1 (
    .a_1(a_1), .b_1(b_1), .s_1(_1bit_adder_1_s_1), .t_1(_1bit_adder_1_t_1), .r_1(_1bit_adder_1_r_1),
    .R_1_2(_1bit_adder_1_r_1_2));
  _1bit_adder _1bit_adder_2 (
    .a_1(a_0), .b_1(b_0), .s_1(s_0), .t_1(t_0), .r_1(_1bit_adder_2_r_1), .R_1_2(_1bit_adder_2_r_1_2));
  not not_1 (not_1_out, _1bit_adder_2_r_1);
  and and_1 (and_1_out, _1bit_adder_1_s_1, not_1_out);
  and and_2 (and_2_out, _1bit_adder_1_t_1, _1bit_adder_2_r_1);
  or or_1 (s_1, and_2_out, and_1_out);
  not not_2 (not_2_out, _1bit_adder_2_r_1_2);
  and and_3 (and_3_out, _1bit_adder_1_s_1, not_2_out);
  and and_4 (and_4_out, _1bit_adder_1_t_1, _1bit_adder_2_r_1_2);
  or or_2 (t_1, and_4_out, and_3_out);
  or or_3 (r_1, and_5_out, _1bit_adder_1_r_1);
  and and_5 (and_5_out, _1bit_adder_1_r_1_2, _1bit_adder_2_r_1);
  and and_6 (and_6_out, _1bit_adder_1_r_1_2, _1bit_adder_2_r_1_2);
  or or_4 (R_1_2, and_6_out, _1bit_adder_1_r_1);
endmodule

/* Test case:
a_1 a_0 b_1 b_0 s_1 s_0 t_1 t_0 r_1 R_1
1   0   0   1     1   1   0   0   0   1
1   1   1   1     1   0   1   1   1   1
1   1   0   1     0   0   0   1   1   1
0   0   0   0     0   0   0   1   0   0
0   0   0   1     0   1   1   0   0   0
*/
