// Digital circuit 4bits_adder.dig as structural Verilog
module _4bits_adder (
  input  a_0,
  input  a_1,
  input  b_0,
  input  b_1,
  input  b_2,
  input  b_3,
  input  a_2,
  input  a_3,
  output s_0,
  output s_1,
  output s_2,
  output s_3,
  output t_0,
  output t_1,
  output t_2,
  output t_3,
  output R_1,
  output r_1_2
);

  wire _2bits_adder_1_r_1, _2bits_adder_1_r_1_2, _2bits_adder_1_s_0, _2bits_adder_1_s_1, _2bits_adder_1_t_0,
       _2bits_adder_1_t_1, _2bits_adder_2_r_1, _2bits_adder_2_r_1_2, and_1_out, and_2_out, and_3_out,
       and_4_out, and_5_out, and_6_out, and_7_out, and_8_out, and_9_out, and_10_out, not_1_out, not_2_out,
       not_3_out, not_4_out;

  _2bits_adder _2bits_adder_1 (
    .a_1(a_3), .a_0(a_2), .b_1(b_3), .b_0(b_2), .s_1(_2bits_adder_1_s_1), .s_0(_2bits_adder_1_s_0),
    .t_1(_2bits_adder_1_t_1), .t_0(_2bits_adder_1_t_0), .r_1(_2bits_adder_1_r_1), .R_1_2(_2bits_adder_1_r_1_2));
  _2bits_adder _2bits_adder_2 (
    .a_1(a_1), .a_0(a_0), .b_1(b_1), .b_0(b_0), .s_1(s_1), .s_0(s_0), .t_1(t_1), .t_0(t_0),
    .r_1(_2bits_adder_2_r_1), .R_1_2(_2bits_adder_2_r_1_2));
  and and_1 (and_1_out, not_1_out, _2bits_adder_1_s_1);
  not not_1 (not_1_out, _2bits_adder_2_r_1);
  not not_2 (not_2_out, _2bits_adder_2_r_1_2);
  and and_2 (and_2_out, _2bits_adder_1_s_1, not_2_out);
  or or_1 (s_3, and_1_out, and_3_out);
  and and_3 (and_3_out, _2bits_adder_2_r_1, _2bits_adder_1_t_1);
  and and_4 (and_4_out, _2bits_adder_1_t_1, _2bits_adder_2_r_1_2);
  or or_2 (t_2, and_4_out, and_2_out);
  and and_5 (and_5_out, not_3_out, _2bits_adder_1_s_0);
  not not_3 (not_3_out, _2bits_adder_2_r_1);
  not not_4 (not_4_out, _2bits_adder_2_r_1_2);
  and and_6 (and_6_out, _2bits_adder_1_s_0, not_4_out);
  or or_3 (s_2, and_5_out, and_7_out);
  and and_7 (and_7_out, _2bits_adder_2_r_1, _2bits_adder_1_t_0);
  and and_8 (and_8_out, _2bits_adder_1_t_0, _2bits_adder_2_r_1_2);
  or or_4 (t_3, and_8_out, and_6_out);
  and and_9 (and_9_out, _2bits_adder_1_r_1_2, _2bits_adder_2_r_1);
  and and_10 (and_10_out, _2bits_adder_1_r_1_2, _2bits_adder_2_r_1_2);
  or or_5 (r_1_2, _2bits_adder_1_r_1, and_9_out);
  or or_6 (R_1, _2bits_adder_1_r_1, and_10_out);
endmodule
