// Digital circuit adder_4bits_copy.dig as structural Verilog
module adder_4bits_copy (
  input  CarryIn,
  input  a_3,
  input  a_2,
  input  a_1,
  input  a_0,
  output o_c,
  output o_1,
  output o_0,
  output o_2,
  output o_3
);

  wire and_1_out, and_2_out, and_3_out;

  and and_1 (and_1_out, a_0, CarryIn);
  and and_2 (and_2_out, a_0, a_1, CarryIn);
  and and_3 (and_3_out, a_0, a_1, a_1, CarryIn);
  and and_4 (o_c, a_0, a_1, a_1, a_3, CarryIn);
  half_adder half_adder_1 (.b(CarryIn), .a(a_0), .Result(o_0));  // open: CarryOut
  half_adder half_adder_2 (.b(and_1_out), .a(a_1), .Result(o_1));  // open: CarryOut
  half_adder half_adder_3 (.b(and_2_out), .a(a_2), .Result(o_2));  // open: CarryOut
  half_adder half_adder_4 (.b(and_3_out), .a(a_3), .Result(o_3));  // open: CarryOut

  // Notes on the sheet:
  //   Component: 4-bit adder (New)
endmodule
