// Digital circuit adder_4bits_copy_delay.dig as structural Verilog
module adder_4bits_copy_delay (
  input  CarryIn,
  input  a_3,
  input  a_2,
  input  a_1,
  input  a_0,
  output o_c,
  output o_1,
  output o_0,
  output o_2,
  output o_3
);

  wire and_1_out, and_2_out, and_3_out, and_4_out, delay_1_out, delay_2_out, delay_3_out;

  and and_1 (and_1_out, a_0, CarryIn);
  and and_2 (and_2_out, a_0, a_1, CarryIn);
  and and_3 (and_3_out, a_0, a_1, a_2, CarryIn);
  and and_4 (and_4_out, a_0, a_1, a_2, a_3, CarryIn);
  Delay delay_1 (.in(and_1_out), .out(delay_1_out));
  Delay delay_2 (.in(and_2_out), .out(delay_2_out));
  Delay delay_3 (.in(and_3_out), .out(delay_3_out));
  Delay delay_4 (.in(and_4_out), .out(o_c));
  half_adder_delay half_adder_delay_1 (.b(CarryIn), .a(a_0), .Result(o_0));  // open: CarryOut
  half_adder_delay half_adder_delay_2 (.b(delay_1_out), .a(a_1), .Result(o_1));  // open: CarryOut
  half_adder_delay half_adder_delay_3 (.b(delay_2_out), .a(a_2), .Result(o_2));  // open: CarryOut
  half_adder_delay half_adder_delay_4 (.b(delay_3_out), .a(a_3), .Result(o_3));  // open: CarryOut
endmodule
