// Digital circuit generate_gp.dig as structural Verilog
module generate_gp (
  input  A_i,
  input  B_i,
  output G_i,
  output P_i
);

  and and_1 (G_i, A_i, B_i);
  or or_1 (P_i, A_i, B_i);

  // Notes on the sheet:
  //   Component: Generation of signal G_i and P_i
endmodule
