// Digital circuit half_adder_delay.dig as structural Verilog
module half_adder_delay (
  input  b,
  input  a,
  output Result,
  output CarryOut
);

  wire and_1_out, xor_1_out;

  xor xor_1 (xor_1_out, b, a);
  and and_1 (and_1_out, b, a);
  Delay delay_1 (.in(xor_1_out), .out(Result));
  Delay delay_2 (.in(and_1_out), .out(CarryOut));
endmodule
