// Digital circuit twos_complement.dig as structural Verilog
module twos_complement (
  input  s_7,
  input  s_6,
  input  s_5,
  input  s_4,
  input  s_3,
  input  s_2,
  input  s_1,
  input  s_0,
  output c_7,
  output c_6,
  output c_5,
  output c_4,
  output c_3,
  output c_2,
  output c_1,
  output c_0
);

  wire half_adder_2_carryout, half_adder_3_carryout, half_adder_4_carryout, half_adder_5_carryout,
       half_adder_6_carryout, half_adder_7_carryout, multiplexer_1_out, multiplexer_2_out, multiplexer_3_out,
       multiplexer_4_out, multiplexer_5_out, multiplexer_6_out, multiplexer_7_out, not_1_out, not_2_out,
       not_3_out, not_4_out, not_5_out, not_6_out, not_7_out;

  not not_1 (not_1_out, s_6);
  Multiplexer multiplexer_1 (.sel(s_7), .in_0(s_6), .in_1(not_1_out), .out(multiplexer_1_out));
  half_adder half_adder_1 (.b(half_adder_2_carryout), .a(multiplexer_1_out), .Result(c_6));  // open: CarryOut
  not not_2 (not_2_out, s_5);
  Multiplexer multiplexer_2 (.sel(s_7), .in_0(s_5), .in_1(not_2_out), .out(multiplexer_2_out));
  half_adder half_adder_2 (
    .b(half_adder_3_carryout), .a(multiplexer_2_out), .Result(c_5), .CarryOut(half_adder_2_carryout));
  not not_3 (not_3_out, s_4);
  Multiplexer multiplexer_3 (.sel(s_7), .in_0(s_4), .in_1(not_3_out), .out(multiplexer_3_out));
  half_adder half_adder_3 (
    .b(half_adder_4_carryout), .a(multiplexer_3_out), .Result(c_4), .CarryOut(half_adder_3_carryout));
  not not_4 (not_4_out, s_3);
  Multiplexer multiplexer_4 (.sel(s_7), .in_0(s_3), .in_1(not_4_out), .out(multiplexer_4_out));
  half_adder half_adder_4 (
    .b(half_adder_5_carryout), .a(multiplexer_4_out), .Result(c_3), .CarryOut(half_adder_4_carryout));
  not not_5 (not_5_out, s_2);
  Multiplexer multiplexer_5 (.sel(s_7), .in_0(s_2), .in_1(not_5_out), .out(multiplexer_5_out));
  half_adder half_adder_5 (
    .b(half_adder_6_carryout), .a(multiplexer_5_out), .Result(c_2), .CarryOut(half_adder_5_carryout));
  not not_6 (not_6_out, s_1);
  Multiplexer multiplexer_6 (.sel(s_7), .in_0(s_1), .in_1(not_6_out), .out(multiplexer_6_out));
  half_adder half_adder_6 (
    .b(half_adder_7_carryout), .a(multiplexer_6_out), .Result(c_1), .CarryOut(half_adder_6_carryout));
  not not_7 (not_7_out, s_0);
  Multiplexer multiplexer_7 (.sel(s_7), .in_0(s_0), .in_1(not_7_out), .out(multiplexer_7_out));
  half_adder half_adder_7 (.b(s_7), .a(multiplexer_7_out), .Result(c_0), .CarryOut(half_adder_7_carryout));

  assign c_7 = s_7;

  // Notes on the sheet:
  //   Question 1
  //   Sign-magnitude representation
  //   Two's complement
endmodule

/* Test case:
s_7 s_6 s_5 s_4 s_3 s_2 s_1 s_0 c_7 c_6 c_5 c_4 c_3 c_2 c_1 c_0
0   0   0   0   0   0   0   1   0   0   0   0   0   0   0   1
0   0   0   0   0   0   1   0   0   0   0   0   0   0   1   0
0   0   0   0   0   1   0   0   0   0   0   0   0   1   0   0
0   0   0   0   1   0   0   0   0   0   0   0   1   0   0   0
0   0   0   1   0   0   0   0   0   0   0   1   0   0   0   0
0   0   1   0   0   0   0   0   0   0   1   0   0   0   0   0
0   1   0   0   0   0   0   0   0   1   0   0   0   0   0   0
1   0   0   0   0   0   0   0   1   0   0   0   0   0   0   0
1   1   1   1   1   1   1   1   1   0   0   0   0   0   0   1
0   1   1   1   1   1   1   1   0   1   1   1   1   1   1   1
1   1   0   0   0   0   0   1   1   0   1   1   1   1   1   1
1   0   1   0   1   0   1   0   1   1   0   1   0   1   1   0
1   0   0   1   0   0   1   0   1   1   1   0   1   1   1   0
*/
