// Digital circuit adder_4bits.dig as structural Verilog
module adder_4bits (
  input  CarryIn,
  input  a_3,
  input  a_2,
  input  a_1,
  input  a_0,
  input  b_3,
  input  b_2,
  input  b_1,
  input  b_0,
  output o_0,
  output o_1,
  output o_2,
  output o_3,
  output o_c
);

  wire and_1_out, and_2_out, and_3_out, and_4_out, and_5_out, and_6_out, and_7_out, and_8_out, and_9_out,
       and_10_out, generate_gp_1_g_i, generate_gp_1_p_i, generate_gp_2_g_i, generate_gp_2_p_i,
       generate_gp_3_g_i, generate_gp_3_p_i, generate_gp_4_g_i, generate_gp_4_p_i, or_1_out, or_2_out,
       or_4_out;

  generate_gp generate_gp_1 (.A_i(a_3), .B_i(b_3), .G_i(generate_gp_1_g_i), .P_i(generate_gp_1_p_i));
  generate_gp generate_gp_2 (.A_i(a_2), .B_i(b_2), .G_i(generate_gp_2_g_i), .P_i(generate_gp_2_p_i));
  generate_gp generate_gp_3 (.A_i(a_1), .B_i(b_1), .G_i(generate_gp_3_g_i), .P_i(generate_gp_3_p_i));
  generate_gp generate_gp_4 (.A_i(a_0), .B_i(b_0), .G_i(generate_gp_4_g_i), .P_i(generate_gp_4_p_i));
  full_adder full_adder_1 (.a(a_0), .b(b_0), .CarryIn(CarryIn), .Result(o_0));  // open: CarryOut
  and and_1 (and_1_out, generate_gp_2_g_i, generate_gp_1_p_i);
  and and_2 (and_2_out, generate_gp_3_g_i, generate_gp_1_p_i, generate_gp_2_p_i);
  and and_3 (and_3_out, generate_gp_4_g_i, generate_gp_1_p_i, generate_gp_2_p_i, generate_gp_3_p_i);
  and and_4 (and_4_out, CarryIn, generate_gp_1_p_i, generate_gp_2_p_i, generate_gp_3_p_i, generate_gp_4_p_i);
  and and_5 (and_5_out, generate_gp_2_p_i, generate_gp_3_g_i);
  and and_6 (and_6_out, generate_gp_2_p_i, generate_gp_3_p_i, generate_gp_4_g_i);
  and and_7 (and_7_out, generate_gp_2_p_i, generate_gp_3_p_i, generate_gp_4_p_i, CarryIn);
  and and_8 (and_8_out, generate_gp_3_p_i, generate_gp_4_g_i);
  and and_9 (and_9_out, generate_gp_4_p_i, generate_gp_3_p_i, CarryIn);
  and and_10 (and_10_out, CarryIn, generate_gp_4_p_i);
  or or_1 (or_1_out, generate_gp_3_g_i, and_8_out, and_9_out);
  or or_2 (or_2_out, and_10_out, generate_gp_4_g_i);
  or or_3 (o_c, generate_gp_1_g_i, and_1_out, and_2_out, and_3_out, and_4_out);
  or or_4 (or_4_out, generate_gp_2_g_i, and_5_out, and_6_out, and_7_out);
  full_adder full_adder_2 (.a(a_2), .b(b_2), .CarryIn(or_1_out), .Result(o_2));  // open: CarryOut
  full_adder full_adder_3 (.a(a_1), .b(b_1), .CarryIn(or_2_out), .Result(o_1));  // open: CarryOut
  full_adder full_adder_4 (.a(a_3), .b(b_3), .CarryIn(or_4_out), .Result(o_3));  // open: CarryOut

  // Notes on the sheet:
  //   Component: 4-bit adder
endmodule
