// Digital circuit full_adder.dig as structural Verilog
module full_adder (
  input  a,
  input  b,
  input  CarryIn,
  output Result,
  output CarryOut
);

  wire and_1_out, and_2_out, and_3_out, or_1_out, xor_1_out;

  xor xor_1 (xor_1_out, a, CarryIn);
  and and_1 (and_1_out, CarryIn, a);
  and and_2 (and_2_out, a, b);
  and and_3 (and_3_out, CarryIn, b);
  xor xor_2 (Result, xor_1_out, b);
  or or_1 (or_1_out, and_1_out, and_2_out);
  or or_2 (CarryOut, or_1_out, and_3_out);
endmodule
