// Digital circuit half_adder.dig as structural Verilog
module half_adder (
  input  b,
  input  a,
  output Result,
  output CarryOut
);

  xor xor_1 (Result, b, a);
  and and_1 (CarryOut, b, a);

  // Notes on the sheet:
  //   Component: Half Adder (Layout 1)
endmodule
