// Digital circuit 1-bit-memory.dig as structural Verilog
module _1_bit_memory (
  input  InputBit,
  input  Select,
  input  Read_Write,
  output OutputBit,
  output Done
);

  wire and_1_out, and_2_out, and_3_out, and_5_out, and_6_out, d_ff_1_q, not_1_out, xnor_1_out, xnor_2_out;

  not not_1 (not_1_out, Read_Write);
  and and_1 (and_1_out, Select, InputBit);
  and and_2 (and_2_out, Read_Write, Select);
  and and_3 (and_3_out, Select, not_1_out);
  D_FF d_ff_1 (.D(and_1_out), .C(and_2_out), .Q(d_ff_1_q));  // open: nQ
  and and_4 (OutputBit, Select, d_ff_1_q);
  xnor xnor_1 (xnor_1_out, d_ff_1_q, InputBit);
  xnor xnor_2 (xnor_2_out, OutputBit, d_ff_1_q);
  and and_5 (and_5_out, xnor_1_out, and_2_out);
  and and_6 (and_6_out, and_3_out, xnor_2_out);
  or or_1 (Done, and_5_out, and_6_out);
endmodule
