// Digital circuit 8-bit-memories.dig as structural Verilog
module _8_bit_memories (
  input  Clk,
  input  SelMemory_0,
  input  SelMemory_1,
  input  SelMemory_2,
  input  InputBit_0,
  input  InputBit_1,
  input  InputBit_2,
  input  InputBit_3,
  input  InputBit_4,
  input  InputBit_5,
  input  InputBit_6,
  input  InputBit_7,
  input  Read_Write,
  input  On_Off,
  output Output_0,
  output Output_1,
  output Output_2,
  output Output_3,
  output Output_4,
  output Output_5,
  output Output_6,
  output Output_7,
  output Done
);

  wire _8_bit_memory_1_done, _8_bit_memory_1_output_0, _8_bit_memory_1_output_1, _8_bit_memory_1_output_2,
       _8_bit_memory_1_output_3, _8_bit_memory_1_output_4, _8_bit_memory_1_output_5,
       _8_bit_memory_1_output_6, _8_bit_memory_1_output_7, _8_bit_memory_2_done, _8_bit_memory_2_output_0,
       _8_bit_memory_2_output_1, _8_bit_memory_2_output_2, _8_bit_memory_2_output_3,
       _8_bit_memory_2_output_4, _8_bit_memory_2_output_5, _8_bit_memory_2_output_6,
       _8_bit_memory_2_output_7, _8_bit_memory_3_done, _8_bit_memory_3_output_0, _8_bit_memory_3_output_1,
       _8_bit_memory_3_output_2, _8_bit_memory_3_output_3, _8_bit_memory_3_output_4,
       _8_bit_memory_3_output_5, _8_bit_memory_3_output_6, _8_bit_memory_3_output_7, and_1_out, and_2_out,
       and_3_out, and_4_out, and_5_out, and_6_out, d_ff_1_q;

  D_FF d_ff_1 (.D(On_Off), .C(Clk), .Q(d_ff_1_q));  // open: nQ
  and and_1 (and_1_out, SelMemory_2, d_ff_1_q);
  and and_2 (and_2_out, SelMemory_1, d_ff_1_q);
  and and_3 (and_3_out, SelMemory_0, d_ff_1_q);
  _8_bit_memory _8_bit_memory_1 (
    .Input_7(InputBit_7), .Input_6(InputBit_6), .Input_5(InputBit_5), .Input_4(InputBit_4),
    .Input_3(InputBit_3), .Input_2(InputBit_2), .Input_1(InputBit_1), .Input_0(InputBit_0),
    .Output_7(_8_bit_memory_1_output_7), .Output_6(_8_bit_memory_1_output_6),
    .Output_5(_8_bit_memory_1_output_5), .Output_4(_8_bit_memory_1_output_4),
    .Output_3(_8_bit_memory_1_output_3), .Output_2(_8_bit_memory_1_output_2),
    .Output_1(_8_bit_memory_1_output_1), .Output_0(_8_bit_memory_1_output_0), .Select(and_1_out),
    .Read_Write(Read_Write), .Done(_8_bit_memory_1_done));
  _8_bit_memory _8_bit_memory_2 (
    .Input_7(InputBit_7), .Input_6(InputBit_6), .Input_5(InputBit_5), .Input_4(InputBit_4),
    .Input_3(InputBit_3), .Input_2(InputBit_2), .Input_1(InputBit_1), .Input_0(InputBit_0),
    .Output_7(_8_bit_memory_2_output_7), .Output_6(_8_bit_memory_2_output_6),
    .Output_5(_8_bit_memory_2_output_5), .Output_4(_8_bit_memory_2_output_4),
    .Output_3(_8_bit_memory_2_output_3), .Output_2(_8_bit_memory_2_output_2),
    .Output_1(_8_bit_memory_2_output_1), .Output_0(_8_bit_memory_2_output_0), .Select(and_2_out),
    .Read_Write(Read_Write), .Done(_8_bit_memory_2_done));
  _8_bit_memory _8_bit_memory_3 (
    .Input_7(InputBit_7), .Input_6(InputBit_6), .Input_5(InputBit_5), .Input_4(InputBit_4),
    .Input_3(InputBit_3), .Input_2(InputBit_2), .Input_1(InputBit_1), .Input_0(InputBit_0),
    .Output_7(_8_bit_memory_3_output_7), .Output_6(_8_bit_memory_3_output_6),
    .Output_5(_8_bit_memory_3_output_5), .Output_4(_8_bit_memory_3_output_4),
    .Output_3(_8_bit_memory_3_output_3), .Output_2(_8_bit_memory_3_output_2),
    .Output_1(_8_bit_memory_3_output_1), .Output_0(_8_bit_memory_3_output_0), .Select(and_3_out),
    .Read_Write(Read_Write), .Done(_8_bit_memory_3_done));
  or or_1 (Output_7, _8_bit_memory_1_output_7, _8_bit_memory_2_output_7, _8_bit_memory_3_output_7);
  or or_2 (Output_6, _8_bit_memory_1_output_6, _8_bit_memory_2_output_6, _8_bit_memory_3_output_6);
  or or_3 (Output_5, _8_bit_memory_1_output_5, _8_bit_memory_2_output_5, _8_bit_memory_3_output_5);
  or or_4 (Output_4, _8_bit_memory_1_output_4, _8_bit_memory_2_output_4, _8_bit_memory_3_output_4);
  or or_5 (Output_3, _8_bit_memory_1_output_3, _8_bit_memory_2_output_3, _8_bit_memory_3_output_3);
  or or_6 (Output_2, _8_bit_memory_1_output_2, _8_bit_memory_2_output_2, _8_bit_memory_3_output_2);
  or or_7 (Output_1, _8_bit_memory_1_output_1, _8_bit_memory_2_output_1, _8_bit_memory_3_output_1);
  or or_8 (Output_0, _8_bit_memory_1_output_0, _8_bit_memory_2_output_0, _8_bit_memory_3_output_0);
  and and_4 (and_4_out, SelMemory_2, _8_bit_memory_1_done);
  and and_5 (and_5_out, SelMemory_1, _8_bit_memory_2_done);
  and and_6 (and_6_out, SelMemory_0, _8_bit_memory_3_done);
  or or_9 (Done, and_4_out, and_5_out, and_6_out);
endmodule
