// Digital circuit 8-bit-memory.dig as structural Verilog
module _8_bit_memory (
  input  Input_0,
  input  Input_1,
  input  Input_2,
  input  Input_3,
  input  Input_4,
  input  Input_5,
  input  Input_6,
  input  Input_7,
  input  Select,
  input  Read_Write,
  output Output_0,
  output Output_1,
  output Output_2,
  output Output_3,
  output Output_4,
  output Output_5,
  output Output_6,
  output Output_7,
  output Done
);

  wire _1_bit_memory_1_done, _1_bit_memory_2_done, _1_bit_memory_3_done, _1_bit_memory_4_done,
       _1_bit_memory_5_done, _1_bit_memory_6_done, _1_bit_memory_7_done, _1_bit_memory_8_done;

  _1_bit_memory _1_bit_memory_1 (
    .InputBit(Input_7), .OutputBit(Output_7), .Select(Select), .Read_Write(Read_Write),
    .Done(_1_bit_memory_1_done));
  _1_bit_memory _1_bit_memory_2 (
    .InputBit(Input_6), .OutputBit(Output_6), .Select(Select), .Read_Write(Read_Write),
    .Done(_1_bit_memory_2_done));
  _1_bit_memory _1_bit_memory_3 (
    .InputBit(Input_5), .OutputBit(Output_5), .Select(Select), .Read_Write(Read_Write),
    .Done(_1_bit_memory_3_done));
  _1_bit_memory _1_bit_memory_4 (
    .InputBit(Input_4), .OutputBit(Output_4), .Select(Select), .Read_Write(Read_Write),
    .Done(_1_bit_memory_4_done));
  _1_bit_memory _1_bit_memory_5 (
    .InputBit(Input_3), .OutputBit(Output_3), .Select(Select), .Read_Write(Read_Write),
    .Done(_1_bit_memory_5_done));
  _1_bit_memory _1_bit_memory_6 (
    .InputBit(Input_2), .OutputBit(Output_2), .Select(Select), .Read_Write(Read_Write),
    .Done(_1_bit_memory_6_done));
  _1_bit_memory _1_bit_memory_7 (
    .InputBit(Input_1), .OutputBit(Output_1), .Select(Select), .Read_Write(Read_Write),
    .Done(_1_bit_memory_7_done));
  _1_bit_memory _1_bit_memory_8 (
    .InputBit(Input_0), .OutputBit(Output_0), .Select(Select), .Read_Write(Read_Write),
    .Done(_1_bit_memory_8_done));
  and and_1 (Done, _1_bit_memory_1_done, _1_bit_memory_2_done, _1_bit_memory_3_done, _1_bit_memory_4_done, _1_bit_memory_5_done, _1_bit_memory_6_done, _1_bit_memory_7_done, _1_bit_memory_8_done);
endmodule
