// Digital circuit 8-bit-register.dig as structural Verilog
module _8_bit_register (
  input  Clk,
  input  i_0,
  input  i_1,
  input  i_2,
  input  i_3,
  input  i_4,
  input  i_5,
  input  i_6,
  input  i_7,
  input  Enable,
  output o_0,
  output o_1,
  output o_2,
  output o_3,
  output o_4,
  output o_5,
  output o_6,
  output o_7
);

  Register register_1 (.D(i_7), .C(Clk), .en(Enable), .Q(o_7));
  Register register_2 (.D(i_6), .C(Clk), .en(Enable), .Q(o_6));
  Register register_3 (.D(i_5), .C(Clk), .en(Enable), .Q(o_5));
  Register register_4 (.D(i_4), .C(Clk), .en(Enable), .Q(o_4));
  Register register_5 (.D(i_3), .C(Clk), .en(Enable), .Q(o_3));
  Register register_6 (.D(i_2), .C(Clk), .en(Enable), .Q(o_2));
  Register register_7 (.D(i_1), .C(Clk), .en(Enable), .Q(o_1));
  Register register_8 (.D(i_0), .C(Clk), .en(Enable), .Q(o_0));
endmodule
