// Digital circuit all-instructions.dig as structural Verilog
module all_instructions (
  input  i_0,
  input  i_1,
  input  i_2,
  input  i_3,
  input  i_4,
  input  i_5,
  input  i_6,
  input  i_7,
  input  LOAD,
  input  STORE,
  input  Fromm_1,
  input  Fromm_2,
  input  Fromm_3,
  input  Fromr_1,
  input  Fromr_2,
  input  Tom_1,
  input  Tom_2,
  input  Tom_3,
  input  Tor_1,
  input  Tor_2,
  input  Clk,
  input  ADD,
  input  SUB,
  input  r1AsOperandb,
  output m1_0,
  output m1_1,
  output m1_2,
  output m1_3,
  output m1_4,
  output m1_5,
  output m1_6,
  output m1_7,
  output m2_0,
  output m2_1,
  output m2_2,
  output m2_3,
  output m2_4,
  output m2_5,
  output m2_6,
  output m2_7,
  output m3_0,
  output m3_1,
  output m3_2,
  output m3_3,
  output m3_4,
  output m3_5,
  output m3_6,
  output m3_7
);

  wire _8_bit_register_1_o_0, _8_bit_register_1_o_1, _8_bit_register_1_o_2, _8_bit_register_1_o_3,
       _8_bit_register_1_o_4, _8_bit_register_1_o_5, _8_bit_register_1_o_6, _8_bit_register_1_o_7,
       _8_bit_register_2_o_0, _8_bit_register_2_o_1, _8_bit_register_2_o_2, _8_bit_register_2_o_3,
       _8_bit_register_2_o_4, _8_bit_register_2_o_5, _8_bit_register_2_o_6, _8_bit_register_2_o_7, alu_1_o_0,
       alu_1_o_1, alu_1_o_2, alu_1_o_3, alu_1_o_4, alu_1_o_5, alu_1_o_6, alu_1_o_7, and_1_out, d_ff_1_q,
       multiplexer_1_out, multiplexer_2_out, multiplexer_3_out, multiplexer_4_out, multiplexer_5_out,
       multiplexer_6_out, multiplexer_7_out, multiplexer_8_out, multiplexer_9_out, multiplexer_10_out,
       multiplexer_11_out, multiplexer_12_out, multiplexer_13_out, multiplexer_14_out, multiplexer_15_out,
       multiplexer_16_out, multiplexer_17_out, multiplexer_18_out, multiplexer_19_out, multiplexer_20_out,
       multiplexer_21_out, multiplexer_22_out, multiplexer_23_out, multiplexer_24_out, multiplexer_25_out,
       multiplexer_26_out, multiplexer_27_out, multiplexer_28_out, multiplexer_29_out, multiplexer_30_out,
       multiplexer_31_out, multiplexer_32_out, multiplexer_33_out, multiplexer_34_out, multiplexer_35_out,
       multiplexer_36_out, multiplexer_37_out, multiplexer_38_out, multiplexer_39_out, multiplexer_40_out,
       or_1_out, or_2_out, or_3_out, or_4_out, or_5_out, or_6_out, or_7_out, or_8_out, or_9_out, or_10_out,
       or_11_out, or_12_out, or_13_out, or_14_out, or_15_out;

  or or_1 (or_1_out, ADD, STORE, LOAD, SUB);
  D_FF d_ff_1 (.D(or_1_out), .C(Clk), .Q(d_ff_1_q));  // open: nQ
  or or_2 (or_2_out, Tom_1, Tom_2, Tom_3);
  or or_3 (or_3_out, Fromr_1, Fromr_2);
  and and_1 (and_1_out, or_2_out, or_3_out);
  or or_4 (or_4_out, Tom_1, Fromm_1);
  Multiplexer multiplexer_1 (.sel(and_1_out), .in_0(i_7), .in_1(multiplexer_33_out), .out(multiplexer_1_out));
  Multiplexer multiplexer_2 (.sel(and_1_out), .in_0(i_6), .in_1(multiplexer_34_out), .out(multiplexer_2_out));
  Multiplexer multiplexer_3 (.sel(and_1_out), .in_0(i_5), .in_1(multiplexer_35_out), .out(multiplexer_3_out));
  Multiplexer multiplexer_4 (.sel(and_1_out), .in_0(i_4), .in_1(multiplexer_36_out), .out(multiplexer_4_out));
  Multiplexer multiplexer_5 (.sel(and_1_out), .in_0(i_3), .in_1(multiplexer_37_out), .out(multiplexer_5_out));
  Multiplexer multiplexer_6 (.sel(and_1_out), .in_0(i_2), .in_1(multiplexer_38_out), .out(multiplexer_6_out));
  Multiplexer multiplexer_7 (.sel(and_1_out), .in_0(i_1), .in_1(multiplexer_39_out), .out(multiplexer_7_out));
  Multiplexer multiplexer_8 (.sel(and_1_out), .in_0(i_0), .in_1(multiplexer_40_out), .out(multiplexer_8_out));
  Multiplexer multiplexer_9 (
    .sel(r1AsOperandb), .in_0(_8_bit_register_1_o_7), .in_1(_8_bit_register_2_o_7), .out(multiplexer_9_out));
  Multiplexer multiplexer_10 (
    .sel(r1AsOperandb), .in_0(_8_bit_register_1_o_6), .in_1(_8_bit_register_2_o_6), .out(multiplexer_10_out));
  Multiplexer multiplexer_11 (
    .sel(r1AsOperandb), .in_0(_8_bit_register_1_o_5), .in_1(_8_bit_register_2_o_5), .out(multiplexer_11_out));
  Multiplexer multiplexer_12 (
    .sel(r1AsOperandb), .in_0(_8_bit_register_1_o_4), .in_1(_8_bit_register_2_o_4), .out(multiplexer_12_out));
  Multiplexer multiplexer_13 (
    .sel(r1AsOperandb), .in_0(_8_bit_register_1_o_3), .in_1(_8_bit_register_2_o_3), .out(multiplexer_13_out));
  Multiplexer multiplexer_14 (
    .sel(r1AsOperandb), .in_0(_8_bit_register_1_o_2), .in_1(_8_bit_register_2_o_2), .out(multiplexer_14_out));
  Multiplexer multiplexer_15 (
    .sel(r1AsOperandb), .in_0(_8_bit_register_1_o_1), .in_1(_8_bit_register_2_o_1), .out(multiplexer_15_out));
  Multiplexer multiplexer_16 (
    .sel(r1AsOperandb), .in_0(_8_bit_register_1_o_0), .in_1(_8_bit_register_2_o_0), .out(multiplexer_16_out));
  or or_5 (or_5_out, Tom_2, Fromm_2);
  _8_bit_memories m_3 (
    .InputBit_7(multiplexer_1_out), .InputBit_6(multiplexer_2_out), .InputBit_5(multiplexer_3_out),
    .InputBit_4(multiplexer_4_out), .InputBit_3(multiplexer_5_out), .InputBit_2(multiplexer_6_out),
    .InputBit_1(multiplexer_7_out), .InputBit_0(multiplexer_8_out), .SelMemory_2(1'b1), .SelMemory_1(1'b0),
    .SelMemory_0(1'b0), .Read_Write(STORE), .Output_7(m1_0), .Output_6(m1_1), .Output_5(m1_2),
    .Output_4(m1_3), .Output_3(m1_4), .Output_2(m1_5), .Output_1(m1_6), .Output_0(m1_7), .Enable(or_4_out));
  alu alu_1 (
    .Sgn(SUB), .i_1_bit_7(multiplexer_9_out), .i_1_bit_6(multiplexer_10_out), .i_1_bit_5(multiplexer_11_out),
    .i_1_bit_4(multiplexer_12_out), .i_1_bit_3(multiplexer_13_out), .i_1_bit_2(multiplexer_14_out),
    .i_1_bit_1(multiplexer_15_out), .i_1_bit_0(multiplexer_16_out), .i_2_bit_7(multiplexer_17_out),
    .i_2_bit_6(multiplexer_18_out), .i_2_bit_5(multiplexer_19_out), .i_2_bit_4(multiplexer_20_out),
    .i_2_bit_3(multiplexer_21_out), .i_2_bit_2(multiplexer_22_out), .i_2_bit_1(multiplexer_23_out),
    .i_2_bit_0(multiplexer_24_out), .o_7(alu_1_o_7), .o_6(alu_1_o_6), .o_5(alu_1_o_5), .o_4(alu_1_o_4),
    .o_3(alu_1_o_3), .o_2(alu_1_o_2), .o_1(alu_1_o_1), .o_0(alu_1_o_0));
  or or_6 (or_6_out, Tom_3, Fromm_3);
  _8_bit_memories m_2 (
    .InputBit_7(multiplexer_1_out), .InputBit_6(multiplexer_2_out), .InputBit_5(multiplexer_3_out),
    .InputBit_4(multiplexer_4_out), .InputBit_3(multiplexer_5_out), .InputBit_2(multiplexer_6_out),
    .InputBit_1(multiplexer_7_out), .InputBit_0(multiplexer_8_out), .SelMemory_2(1'b1), .SelMemory_1(1'b0),
    .SelMemory_0(1'b0), .Read_Write(STORE), .Output_7(m2_0), .Output_6(m2_1), .Output_5(m2_2),
    .Output_4(m2_3), .Output_3(m2_4), .Output_2(m2_5), .Output_1(m2_6), .Output_0(m2_7), .Enable(or_5_out));
  Multiplexer multiplexer_17 (
    .sel(r1AsOperandb), .in_0(_8_bit_register_2_o_7), .in_1(_8_bit_register_1_o_7), .out(multiplexer_17_out));
  Multiplexer multiplexer_18 (
    .sel(r1AsOperandb), .in_0(_8_bit_register_2_o_6), .in_1(_8_bit_register_1_o_6), .out(multiplexer_18_out));
  Multiplexer multiplexer_19 (
    .sel(r1AsOperandb), .in_0(_8_bit_register_2_o_5), .in_1(_8_bit_register_1_o_5), .out(multiplexer_19_out));
  Multiplexer multiplexer_20 (
    .sel(r1AsOperandb), .in_0(_8_bit_register_2_o_4), .in_1(_8_bit_register_1_o_4), .out(multiplexer_20_out));
  Multiplexer multiplexer_21 (
    .sel(r1AsOperandb), .in_0(_8_bit_register_2_o_3), .in_1(_8_bit_register_1_o_3), .out(multiplexer_21_out));
  Multiplexer multiplexer_22 (
    .sel(r1AsOperandb), .in_0(_8_bit_register_2_o_2), .in_1(_8_bit_register_1_o_2), .out(multiplexer_22_out));
  Multiplexer multiplexer_23 (
    .sel(r1AsOperandb), .in_0(_8_bit_register_2_o_1), .in_1(_8_bit_register_1_o_1), .out(multiplexer_23_out));
  Multiplexer multiplexer_24 (
    .sel(r1AsOperandb), .in_0(_8_bit_register_2_o_0), .in_1(_8_bit_register_1_o_0), .out(multiplexer_24_out));
  or or_7 (or_7_out, m3_0, m2_0, m1_0);
  or or_8 (or_8_out, m3_1, m2_1, m1_1);
  or or_9 (or_9_out, m3_2, m2_2, m1_2);
  or or_10 (or_10_out, m3_3, m2_3, m1_3);
  or or_11 (or_11_out, m3_4, m2_4, m1_4);
  or or_12 (or_12_out, m3_5, m2_5, m1_5);
  or or_13 (or_13_out, m3_6, m2_6, m1_6);
  or or_14 (or_14_out, m3_7, m2_7, m1_7);
  _8_bit_memories m_1 (
    .InputBit_7(multiplexer_1_out), .InputBit_6(multiplexer_2_out), .InputBit_5(multiplexer_3_out),
    .InputBit_4(multiplexer_4_out), .InputBit_3(multiplexer_5_out), .InputBit_2(multiplexer_6_out),
    .InputBit_1(multiplexer_7_out), .InputBit_0(multiplexer_8_out), .SelMemory_2(1'b1), .SelMemory_1(1'b0),
    .SelMemory_0(1'b0), .Read_Write(STORE), .Output_7(m3_0), .Output_6(m3_1), .Output_5(m3_2),
    .Output_4(m3_3), .Output_3(m3_4), .Output_2(m3_5), .Output_1(m3_6), .Output_0(m3_7), .Enable(or_6_out));
  or or_15 (or_15_out, ADD, SUB);
  Multiplexer multiplexer_25 (.sel(or_15_out), .in_0(or_7_out), .in_1(alu_1_o_7), .out(multiplexer_25_out));
  Multiplexer multiplexer_26 (.sel(or_15_out), .in_0(or_8_out), .in_1(alu_1_o_6), .out(multiplexer_26_out));
  Multiplexer multiplexer_27 (.sel(or_15_out), .in_0(or_9_out), .in_1(alu_1_o_5), .out(multiplexer_27_out));
  Multiplexer multiplexer_28 (.sel(or_15_out), .in_0(or_10_out), .in_1(alu_1_o_4), .out(multiplexer_28_out));
  Multiplexer multiplexer_29 (.sel(or_15_out), .in_0(or_11_out), .in_1(alu_1_o_3), .out(multiplexer_29_out));
  Multiplexer multiplexer_30 (.sel(or_15_out), .in_0(or_12_out), .in_1(alu_1_o_2), .out(multiplexer_30_out));
  Multiplexer multiplexer_31 (.sel(or_15_out), .in_0(or_13_out), .in_1(alu_1_o_1), .out(multiplexer_31_out));
  Multiplexer multiplexer_32 (.sel(or_15_out), .in_0(or_14_out), .in_1(alu_1_o_0), .out(multiplexer_32_out));
  Multiplexer multiplexer_33 (
    .sel(Fromr_2), .in_0(_8_bit_register_1_o_7), .in_1(_8_bit_register_2_o_7), .out(multiplexer_33_out));
  Multiplexer multiplexer_34 (
    .sel(Fromr_2), .in_0(_8_bit_register_1_o_6), .in_1(_8_bit_register_2_o_6), .out(multiplexer_34_out));
  Multiplexer multiplexer_35 (
    .sel(Fromr_2), .in_0(_8_bit_register_1_o_5), .in_1(_8_bit_register_2_o_5), .out(multiplexer_35_out));
  Multiplexer multiplexer_36 (
    .sel(Fromr_2), .in_0(_8_bit_register_1_o_4), .in_1(_8_bit_register_2_o_4), .out(multiplexer_36_out));
  Multiplexer multiplexer_37 (
    .sel(Fromr_2), .in_0(_8_bit_register_1_o_3), .in_1(_8_bit_register_2_o_3), .out(multiplexer_37_out));
  Multiplexer multiplexer_38 (
    .sel(Fromr_2), .in_0(_8_bit_register_1_o_2), .in_1(_8_bit_register_2_o_2), .out(multiplexer_38_out));
  Multiplexer multiplexer_39 (
    .sel(Fromr_2), .in_0(_8_bit_register_1_o_1), .in_1(_8_bit_register_2_o_1), .out(multiplexer_39_out));
  Multiplexer multiplexer_40 (
    .sel(Fromr_2), .in_0(_8_bit_register_1_o_0), .in_1(_8_bit_register_2_o_0), .out(multiplexer_40_out));
  _8_bit_register _8_bit_register_1 (
    .Clk(d_ff_1_q), .i_7(multiplexer_25_out), .i_6(multiplexer_26_out), .i_5(multiplexer_27_out),
    .i_4(multiplexer_28_out), .i_3(multiplexer_29_out), .i_2(multiplexer_30_out), .i_1(multiplexer_31_out),
    .i_0(multiplexer_32_out), .Enable(Tor_1), .o_7(_8_bit_register_1_o_7), .o_6(_8_bit_register_1_o_6),
    .o_5(_8_bit_register_1_o_5), .o_4(_8_bit_register_1_o_4), .o_3(_8_bit_register_1_o_3),
    .o_2(_8_bit_register_1_o_2), .o_1(_8_bit_register_1_o_1), .o_0(_8_bit_register_1_o_0));
  _8_bit_register _8_bit_register_2 (
    .Clk(d_ff_1_q), .i_7(multiplexer_25_out), .i_6(multiplexer_26_out), .i_5(multiplexer_27_out),
    .i_4(multiplexer_28_out), .i_3(multiplexer_29_out), .i_2(multiplexer_30_out), .i_1(multiplexer_31_out),
    .i_0(multiplexer_32_out), .Enable(Tor_2), .o_7(_8_bit_register_2_o_7), .o_6(_8_bit_register_2_o_6),
    .o_5(_8_bit_register_2_o_5), .o_4(_8_bit_register_2_o_4), .o_3(_8_bit_register_2_o_3),
    .o_2(_8_bit_register_2_o_2), .o_1(_8_bit_register_2_o_1), .o_0(_8_bit_register_2_o_0));

  // Notes on the sheet:
  //   Instruction Section
  //   ALU Section
  //   Memory Section
  //   Value stored in m_1
  //   Value stored in m_2
  //   Value stored in m_3
  //   Register Section
endmodule
