// Digital circuit all.dig as structural Verilog
module all (
  input  i_0,
  input  i_1,
  input  i_2,
  input  i_3,
  input  i_4,
  input  i_5,
  input  i_6,
  input  i_7,
  input  LOAD,
  input  ADD,
  input  SUB,
  input  STORE,
  input  Fromm_1,
  input  Fromm_2,
  input  Fromm_3,
  input  Fromr_1,
  input  Fromr_2,
  input  Clk,
  input  Tom_1,
  input  Tom_2,
  input  Tom_3,
  input  Tor_1,
  input  Tor_2
);

  wire _8_bit_memories_1_output_0, _8_bit_memories_1_output_1, _8_bit_memories_1_output_2,
       _8_bit_memories_1_output_3, _8_bit_memories_1_output_4, _8_bit_memories_1_output_5,
       _8_bit_memories_1_output_6, _8_bit_memories_1_output_7, _8_bit_memories_2_output_0,
       _8_bit_memories_2_output_1, _8_bit_memories_2_output_2, _8_bit_memories_2_output_3,
       _8_bit_memories_2_output_4, _8_bit_memories_2_output_5, _8_bit_memories_2_output_6,
       _8_bit_memories_2_output_7, _8_bit_memories_3_output_0, _8_bit_memories_3_output_1,
       _8_bit_memories_3_output_2, _8_bit_memories_3_output_3, _8_bit_memories_3_output_4,
       _8_bit_memories_3_output_5, _8_bit_memories_3_output_6, _8_bit_memories_3_output_7,
       _8_bit_register_1_o_0, _8_bit_register_1_o_1, _8_bit_register_1_o_2, _8_bit_register_1_o_3,
       _8_bit_register_1_o_4, _8_bit_register_1_o_5, _8_bit_register_1_o_6, _8_bit_register_1_o_7,
       _8_bit_register_2_o_0, _8_bit_register_2_o_1, _8_bit_register_2_o_2, _8_bit_register_2_o_3,
       _8_bit_register_2_o_4, _8_bit_register_2_o_5, _8_bit_register_2_o_6, _8_bit_register_2_o_7, alu_1_o_0,
       alu_1_o_1, alu_1_o_2, alu_1_o_3, alu_1_o_4, alu_1_o_5, alu_1_o_6, alu_1_o_7, and_1_out, and_2_out,
       d_ff_1_q, multiplexer_1_out, multiplexer_2_out, multiplexer_3_out, multiplexer_4_out,
       multiplexer_5_out, multiplexer_6_out, multiplexer_7_out, multiplexer_8_out, multiplexer_9_out,
       multiplexer_10_out, multiplexer_11_out, multiplexer_12_out, multiplexer_13_out, multiplexer_14_out,
       multiplexer_15_out, multiplexer_16_out, multiplexer_17_out, multiplexer_18_out, multiplexer_19_out,
       multiplexer_20_out, multiplexer_21_out, multiplexer_22_out, multiplexer_23_out, multiplexer_24_out,
       or_1_out, or_2_out, or_3_out, or_4_out, or_5_out, or_6_out, or_7_out, or_8_out, or_9_out, or_10_out,
       or_11_out, or_12_out, or_13_out, or_14_out, or_15_out, or_16_out;

  or or_1 (or_1_out, LOAD, ADD, SUB, STORE);
  D_FF d_ff_1 (.D(or_1_out), .C(Clk), .Q(d_ff_1_q));  // open: nQ
  or or_2 (or_2_out, Fromr_1, Fromr_2);
  or or_3 (or_3_out, Tom_1, Tom_2, Tom_3);
  Multiplexer multiplexer_1 (.sel(and_1_out), .in_0(i_7), .in_1(multiplexer_24_out), .out(multiplexer_1_out));
  Multiplexer multiplexer_2 (.sel(and_1_out), .in_0(i_6), .in_1(multiplexer_23_out), .out(multiplexer_2_out));
  Multiplexer multiplexer_3 (.sel(and_1_out), .in_0(i_5), .in_1(multiplexer_22_out), .out(multiplexer_3_out));
  Multiplexer multiplexer_4 (.sel(and_1_out), .in_0(i_4), .in_1(multiplexer_21_out), .out(multiplexer_4_out));
  Multiplexer multiplexer_5 (.sel(and_1_out), .in_0(i_3), .in_1(multiplexer_20_out), .out(multiplexer_5_out));
  Multiplexer multiplexer_6 (.sel(and_1_out), .in_0(i_2), .in_1(multiplexer_19_out), .out(multiplexer_6_out));
  Multiplexer multiplexer_7 (.sel(and_1_out), .in_0(i_1), .in_1(multiplexer_18_out), .out(multiplexer_7_out));
  Multiplexer multiplexer_8 (.sel(and_1_out), .in_0(i_0), .in_1(multiplexer_17_out), .out(multiplexer_8_out));
  and and_1 (and_1_out, or_2_out, or_3_out);
  _8_bit_memories _8_bit_memories_1 (
    .InputBit_7(multiplexer_1_out), .InputBit_6(multiplexer_2_out), .InputBit_5(multiplexer_3_out),
    .InputBit_4(multiplexer_4_out), .InputBit_3(multiplexer_5_out), .InputBit_2(multiplexer_6_out),
    .InputBit_1(multiplexer_7_out), .InputBit_0(multiplexer_8_out), .SelMemory_2(1'b1), .SelMemory_1(1'b0),
    .SelMemory_0(1'b0), .Read_Write(STORE), .Output_7(_8_bit_memories_1_output_7),
    .Output_6(_8_bit_memories_1_output_6), .Output_5(_8_bit_memories_1_output_5),
    .Output_4(_8_bit_memories_1_output_4), .Output_3(_8_bit_memories_1_output_3),
    .Output_2(_8_bit_memories_1_output_2), .Output_1(_8_bit_memories_1_output_1),
    .Output_0(_8_bit_memories_1_output_0), .Enable(or_4_out));
  or or_4 (or_4_out, Fromm_1, Tom_1);
  _8_bit_memories _8_bit_memories_2 (
    .InputBit_7(multiplexer_1_out), .InputBit_6(multiplexer_2_out), .InputBit_5(multiplexer_3_out),
    .InputBit_4(multiplexer_4_out), .InputBit_3(multiplexer_5_out), .InputBit_2(multiplexer_6_out),
    .InputBit_1(multiplexer_7_out), .InputBit_0(multiplexer_8_out), .SelMemory_2(1'b1), .SelMemory_1(1'b0),
    .SelMemory_0(1'b0), .Read_Write(STORE), .Output_7(_8_bit_memories_2_output_7),
    .Output_6(_8_bit_memories_2_output_6), .Output_5(_8_bit_memories_2_output_5),
    .Output_4(_8_bit_memories_2_output_4), .Output_3(_8_bit_memories_2_output_3),
    .Output_2(_8_bit_memories_2_output_2), .Output_1(_8_bit_memories_2_output_1),
    .Output_0(_8_bit_memories_2_output_0), .Enable(or_5_out));
  or or_5 (or_5_out, Fromm_2, Tom_2);
  _8_bit_memories _8_bit_memories_3 (
    .InputBit_7(multiplexer_1_out), .InputBit_6(multiplexer_2_out), .InputBit_5(multiplexer_3_out),
    .InputBit_4(multiplexer_4_out), .InputBit_3(multiplexer_5_out), .InputBit_2(multiplexer_6_out),
    .InputBit_1(multiplexer_7_out), .InputBit_0(multiplexer_8_out), .SelMemory_2(1'b1), .SelMemory_1(1'b0),
    .SelMemory_0(1'b0), .Read_Write(STORE), .Output_7(_8_bit_memories_3_output_7),
    .Output_6(_8_bit_memories_3_output_6), .Output_5(_8_bit_memories_3_output_5),
    .Output_4(_8_bit_memories_3_output_4), .Output_3(_8_bit_memories_3_output_3),
    .Output_2(_8_bit_memories_3_output_2), .Output_1(_8_bit_memories_3_output_1),
    .Output_0(_8_bit_memories_3_output_0), .Enable(or_6_out));
  or or_6 (or_6_out, Fromm_3, Tom_3);
  or or_7 (or_7_out, _8_bit_memories_3_output_0, _8_bit_memories_2_output_0, _8_bit_memories_1_output_0);
  or or_8 (or_8_out, _8_bit_memories_3_output_1, _8_bit_memories_2_output_1, _8_bit_memories_1_output_1);
  or or_9 (or_9_out, _8_bit_memories_3_output_2, _8_bit_memories_2_output_2, _8_bit_memories_1_output_2);
  or or_10 (or_10_out, _8_bit_memories_3_output_3, _8_bit_memories_2_output_3, _8_bit_memories_1_output_3);
  or or_11 (or_11_out, _8_bit_memories_3_output_4, _8_bit_memories_2_output_4, _8_bit_memories_1_output_4);
  or or_12 (or_12_out, _8_bit_memories_3_output_5, _8_bit_memories_2_output_5, _8_bit_memories_1_output_5);
  or or_13 (or_13_out, _8_bit_memories_3_output_6, _8_bit_memories_2_output_6, _8_bit_memories_1_output_6);
  or or_14 (or_14_out, _8_bit_memories_3_output_7, _8_bit_memories_2_output_7, _8_bit_memories_1_output_7);
  alu alu_1 (
    .Sgn(SUB), .i_1_bit_7(_8_bit_register_1_o_7), .i_1_bit_6(_8_bit_register_1_o_6),
    .i_1_bit_5(_8_bit_register_1_o_5), .i_1_bit_4(_8_bit_register_1_o_4), .i_1_bit_3(_8_bit_register_1_o_3),
    .i_1_bit_2(_8_bit_register_1_o_2), .i_1_bit_1(_8_bit_register_1_o_1), .i_1_bit_0(_8_bit_register_1_o_0),
    .i_2_bit_7(_8_bit_register_2_o_7), .i_2_bit_6(_8_bit_register_2_o_6), .i_2_bit_5(_8_bit_register_2_o_5),
    .i_2_bit_4(_8_bit_register_2_o_4), .i_2_bit_3(_8_bit_register_2_o_3), .i_2_bit_2(_8_bit_register_2_o_2),
    .i_2_bit_1(_8_bit_register_2_o_1), .i_2_bit_0(_8_bit_register_2_o_0), .o_7(alu_1_o_7), .o_6(alu_1_o_6),
    .o_5(alu_1_o_5), .o_4(alu_1_o_4), .o_3(alu_1_o_3), .o_2(alu_1_o_2), .o_1(alu_1_o_1), .o_0(alu_1_o_0));
  or or_15 (or_15_out, Fromm_1, Fromm_2, Fromm_3);
  or or_16 (or_16_out, Tor_1, Tor_2);
  and and_2 (and_2_out, or_15_out, or_16_out);
  Multiplexer multiplexer_9 (.sel(and_2_out), .in_0(alu_1_o_0), .in_1(or_7_out), .out(multiplexer_9_out));
  Multiplexer multiplexer_10 (.sel(and_2_out), .in_0(alu_1_o_1), .in_1(or_8_out), .out(multiplexer_10_out));
  Multiplexer multiplexer_11 (.sel(and_2_out), .in_0(alu_1_o_2), .in_1(or_9_out), .out(multiplexer_11_out));
  Multiplexer multiplexer_12 (.sel(and_2_out), .in_0(alu_1_o_3), .in_1(or_10_out), .out(multiplexer_12_out));
  Multiplexer multiplexer_13 (.sel(and_2_out), .in_0(alu_1_o_4), .in_1(or_11_out), .out(multiplexer_13_out));
  Multiplexer multiplexer_14 (.sel(and_2_out), .in_0(alu_1_o_5), .in_1(or_12_out), .out(multiplexer_14_out));
  Multiplexer multiplexer_15 (.sel(and_2_out), .in_0(alu_1_o_6), .in_1(or_13_out), .out(multiplexer_15_out));
  Multiplexer multiplexer_16 (.sel(and_2_out), .in_0(alu_1_o_7), .in_1(or_14_out), .out(multiplexer_16_out));
  Multiplexer multiplexer_17 (
    .sel(and_1_out), .in_0(_8_bit_register_1_o_0), .in_1(_8_bit_register_2_o_0), .out(multiplexer_17_out));
  Multiplexer multiplexer_18 (
    .sel(and_1_out), .in_0(_8_bit_register_1_o_1), .in_1(_8_bit_register_2_o_1), .out(multiplexer_18_out));
  Multiplexer multiplexer_19 (
    .sel(and_1_out), .in_0(_8_bit_register_1_o_2), .in_1(_8_bit_register_2_o_2), .out(multiplexer_19_out));
  Multiplexer multiplexer_20 (
    .sel(and_1_out), .in_0(_8_bit_register_1_o_3), .in_1(_8_bit_register_2_o_3), .out(multiplexer_20_out));
  Multiplexer multiplexer_21 (
    .sel(and_1_out), .in_0(_8_bit_register_1_o_4), .in_1(_8_bit_register_2_o_4), .out(multiplexer_21_out));
  Multiplexer multiplexer_22 (
    .sel(and_1_out), .in_0(_8_bit_register_1_o_5), .in_1(_8_bit_register_2_o_5), .out(multiplexer_22_out));
  Multiplexer multiplexer_23 (
    .sel(and_1_out), .in_0(_8_bit_register_1_o_6), .in_1(_8_bit_register_2_o_6), .out(multiplexer_23_out));
  Multiplexer multiplexer_24 (
    .sel(and_1_out), .in_0(_8_bit_register_1_o_7), .in_1(_8_bit_register_2_o_7), .out(multiplexer_24_out));
  _8_bit_register _8_bit_register_1 (
    .Clk(d_ff_1_q), .i_7(multiplexer_16_out), .i_6(multiplexer_15_out), .i_5(multiplexer_14_out),
    .i_4(multiplexer_13_out), .i_3(multiplexer_12_out), .i_2(multiplexer_11_out), .i_1(multiplexer_10_out),
    .i_0(multiplexer_9_out), .Enable(Tor_1), .o_7(_8_bit_register_1_o_7), .o_6(_8_bit_register_1_o_6),
    .o_5(_8_bit_register_1_o_5), .o_4(_8_bit_register_1_o_4), .o_3(_8_bit_register_1_o_3),
    .o_2(_8_bit_register_1_o_2), .o_1(_8_bit_register_1_o_1), .o_0(_8_bit_register_1_o_0));
  _8_bit_register _8_bit_register_2 (
    .Clk(d_ff_1_q), .i_7(multiplexer_16_out), .i_6(multiplexer_15_out), .i_5(multiplexer_14_out),
    .i_4(multiplexer_13_out), .i_3(multiplexer_12_out), .i_2(multiplexer_11_out), .i_1(multiplexer_10_out),
    .i_0(multiplexer_9_out), .Enable(Tor_2), .o_7(_8_bit_register_2_o_7), .o_6(_8_bit_register_2_o_6),
    .o_5(_8_bit_register_2_o_5), .o_4(_8_bit_register_2_o_4), .o_3(_8_bit_register_2_o_3),
    .o_2(_8_bit_register_2_o_2), .o_1(_8_bit_register_2_o_1), .o_0(_8_bit_register_2_o_0));
endmodule
