// Digital circuit alu.dig as structural Verilog
module alu (
  input  i_1_bit_0,
  input  i_1_bit_1,
  input  i_1_bit_2,
  input  i_1_bit_3,
  input  i_1_bit_4,
  input  i_1_bit_5,
  input  i_1_bit_6,
  input  i_1_bit_7,
  input  i_2_bit_0,
  input  i_2_bit_1,
  input  i_2_bit_2,
  input  i_2_bit_3,
  input  i_2_bit_4,
  input  i_2_bit_5,
  input  i_2_bit_6,
  input  i_2_bit_7,
  input  Clk,
  input  On_Off,
  output Done,
  output o_bit_0,
  output o_bit_1,
  output o_bit_2,
  output o_bit_3,
  output o_bit_4,
  output o_bit_5,
  output o_bit_6,
  output o_bit_7
);

  D_FF d_ff_1 (.D(On_Off), .C(Clk), .Q(Done));  // open: nQ

  assign o_bit_0 = i_2_bit_0;
  assign o_bit_1 = i_2_bit_1;
  assign o_bit_2 = i_2_bit_2;
  assign o_bit_3 = i_2_bit_3;
  assign o_bit_4 = i_2_bit_4;
  assign o_bit_5 = i_2_bit_5;
  assign o_bit_6 = i_2_bit_6;
  assign o_bit_7 = i_2_bit_7;
endmodule
