// Digital circuit load+store.dig as structural Verilog
module load_store (
  input  StoreInput_0,
  input  StoreInput_1,
  input  StoreInput_2,
  input  StoreInput_3,
  input  StoreInput_4,
  input  StoreInput_5,
  input  StoreInput_6,
  input  StoreInput_7,
  input  StoreMem_0,
  input  StoreMem_1,
  input  StoreMem_2,
  input  StoreMem_3,
  input  Store,
  input  LoadMem_0,
  input  LoadMem_1,
  input  LoadMem_2,
  input  LoadMem_3,
  input  Load,
  input  clk
);

  wire _8_bit_memories_1_output_0, _8_bit_memories_1_output_1, _8_bit_memories_1_output_2,
       _8_bit_memories_1_output_3, _8_bit_memories_1_output_4, _8_bit_memories_1_output_5,
       _8_bit_memories_1_output_6, _8_bit_memories_1_output_7, _8_bit_register_1_o_0, _8_bit_register_1_o_1,
       _8_bit_register_1_o_2, _8_bit_register_1_o_3, _8_bit_register_1_o_4, _8_bit_register_1_o_5,
       _8_bit_register_1_o_6, _8_bit_register_1_o_7, and_1_out, and_2_out, and_3_out, and_4_out,
       multiplexer_1_out, multiplexer_2_out, multiplexer_3_out, multiplexer_4_out, or_1_out;

  and and_1 (and_1_out, Store, clk);
  and and_2 (and_2_out, Load, clk);
  Multiplexer multiplexer_1 (.sel(and_2_out), .in_0(StoreMem_0), .in_1(LoadMem_0), .out(multiplexer_1_out));
  Multiplexer multiplexer_2 (.sel(and_2_out), .in_0(StoreMem_1), .in_1(LoadMem_1), .out(multiplexer_2_out));
  Multiplexer multiplexer_3 (.sel(and_2_out), .in_0(StoreMem_2), .in_1(LoadMem_2), .out(multiplexer_3_out));
  Multiplexer multiplexer_4 (.sel(and_2_out), .in_0(StoreMem_3), .in_1(LoadMem_3), .out(multiplexer_4_out));
  _8_bit_memories _8_bit_memories_1 (
    .Clk(clk), .InputBit_7(StoreInput_7), .InputBit_6(StoreInput_6), .InputBit_5(StoreInput_5),
    .InputBit_4(StoreInput_4), .InputBit_3(StoreInput_3), .InputBit_2(StoreInput_2),
    .InputBit_1(StoreInput_1), .InputBit_0(StoreInput_0), .SelMemory_2(multiplexer_4_out),
    .SelMemory_1(multiplexer_3_out), .SelMemory_0(multiplexer_2_out), .Read_Write(multiplexer_1_out),
    .On_Off(or_1_out), .Output_7(_8_bit_memories_1_output_7), .Output_6(_8_bit_memories_1_output_6),
    .Output_5(_8_bit_memories_1_output_5), .Output_4(_8_bit_memories_1_output_4),
    .Output_3(_8_bit_memories_1_output_3), .Output_2(_8_bit_memories_1_output_2),
    .Output_1(_8_bit_memories_1_output_1), .Output_0(_8_bit_memories_1_output_0));  // open: Done
  or or_1 (or_1_out, and_3_out, and_4_out);
  and and_3 (and_3_out, and_1_out, clk);
  and and_4 (and_4_out, and_2_out, clk);
  _8_bit_register _8_bit_register_1 (
    .Clk(clk), .i_7(_8_bit_memories_1_output_7), .i_6(_8_bit_memories_1_output_6),
    .i_5(_8_bit_memories_1_output_5), .i_4(_8_bit_memories_1_output_4), .i_3(_8_bit_memories_1_output_3),
    .i_2(_8_bit_memories_1_output_2), .i_1(_8_bit_memories_1_output_1), .i_0(_8_bit_memories_1_output_0),
    .Enable(and_4_out), .o_7(_8_bit_register_1_o_7), .o_6(_8_bit_register_1_o_6),
    .o_5(_8_bit_register_1_o_5), .o_4(_8_bit_register_1_o_4), .o_3(_8_bit_register_1_o_3),
    .o_2(_8_bit_register_1_o_2), .o_1(_8_bit_register_1_o_1), .o_0(_8_bit_register_1_o_0));
  LED led_1 (.in(_8_bit_register_1_o_7));
  LED led_2 (.in(_8_bit_register_1_o_6));
  LED led_3 (.in(_8_bit_register_1_o_5));
  LED led_4 (.in(_8_bit_register_1_o_4));
  LED led_5 (.in(_8_bit_register_1_o_3));
  LED led_6 (.in(_8_bit_register_1_o_2));
  LED led_7 (.in(_8_bit_register_1_o_1));
  LED led_8 (.in(_8_bit_register_1_o_0));
endmodule
