// Digital circuit load.dig as structural Verilog
module load (
  input  i_0,
  input  i_1,
  input  i_2,
  input  i_3,
  input  i_4,
  input  i_5,
  input  i_6,
  input  i_7,
  input  Storem_0,
  input  Storem_1,
  input  Storem_2,
  input  r_w,
  input  Clk,
  input  Loadm_0,
  input  on_off,
  input  Loadm_1,
  input  Loadm_2,
  output o_0,
  output o_1,
  output o_2,
  output o_3,
  output o_4,
  output o_5,
  output o_6,
  output o_7
);

  wire _8_bit_memories_1_done, _8_bit_memories_1_output_0, _8_bit_memories_1_output_1,
       _8_bit_memories_1_output_2, _8_bit_memories_1_output_3, _8_bit_memories_1_output_4,
       _8_bit_memories_1_output_5, _8_bit_memories_1_output_6, _8_bit_memories_1_output_7, and_1_out,
       d_ff_1_q, multiplexer_1_out, multiplexer_2_out, multiplexer_3_out;

  Multiplexer multiplexer_1 (.sel(on_off), .in_0(Loadm_0), .in_1(Storem_0), .out(multiplexer_1_out));
  Multiplexer multiplexer_2 (.sel(on_off), .in_0(Loadm_1), .in_1(Storem_1), .out(multiplexer_2_out));
  Multiplexer multiplexer_3 (.sel(on_off), .in_0(Loadm_2), .in_1(Storem_2), .out(multiplexer_3_out));
  _8_bit_memories _8_bit_memories_1 (
    .Clk(Clk), .InputBit_7(i_7), .InputBit_6(i_6), .InputBit_5(i_5), .InputBit_4(i_4), .InputBit_3(i_3),
    .InputBit_2(i_2), .InputBit_1(i_1), .InputBit_0(i_0), .SelMemory_2(multiplexer_3_out),
    .SelMemory_1(multiplexer_2_out), .SelMemory_0(multiplexer_1_out), .Read_Write(r_w), .On_Off(on_off),
    .Output_7(_8_bit_memories_1_output_7), .Output_6(_8_bit_memories_1_output_6),
    .Output_5(_8_bit_memories_1_output_5), .Output_4(_8_bit_memories_1_output_4),
    .Output_3(_8_bit_memories_1_output_3), .Output_2(_8_bit_memories_1_output_2),
    .Output_1(_8_bit_memories_1_output_1), .Output_0(_8_bit_memories_1_output_0),
    .Done(_8_bit_memories_1_done));
  and and_1 (and_1_out, _8_bit_memories_1_done, on_off);
  _8_bit_register _8_bit_register_1 (
    .Clk(Clk), .i_7(_8_bit_memories_1_output_7), .i_6(_8_bit_memories_1_output_6),
    .i_5(_8_bit_memories_1_output_5), .i_4(_8_bit_memories_1_output_4), .i_3(_8_bit_memories_1_output_3),
    .i_2(_8_bit_memories_1_output_2), .i_1(_8_bit_memories_1_output_1), .i_0(_8_bit_memories_1_output_0),
    .Enable(d_ff_1_q), .o_7(o_7), .o_6(o_6), .o_5(o_5), .o_4(o_4), .o_3(o_3), .o_2(o_2), .o_1(o_1), .o_0(o_0));
  D_FF d_ff_1 (.D(and_1_out), .C(Clk), .Q(d_ff_1_q));  // open: nQ

  // Notes on the sheet:
  //   Store Instruction
  //   Load Instruction
endmodule
