// Digital circuit store.dig as structural Verilog
module store (
  input  i_0,
  input  i_1,
  input  i_2,
  input  i_3,
  input  i_4,
  input  i_5,
  input  i_6,
  input  i_7,
  input  m_00,
  input  m_01,
  input  m_02,
  input  Clk,
  input  On_Off,
  input  m_10,
  input  m_11,
  input  m_12,
  input  m_20,
  input  m_21,
  input  m_22
);

  wire d_ff_1_q;

  D_FF d_ff_1 (.D(On_Off), .C(Clk), .Q(d_ff_1_q));  // open: nQ
  _8_bit_memories _8_bit_memories_1 (
    .Clk(d_ff_1_q), .InputBit_7(i_7), .InputBit_6(i_6), .InputBit_5(i_5), .InputBit_4(i_4), .InputBit_3(i_3),
    .InputBit_2(i_2), .InputBit_1(i_1), .InputBit_0(i_0), .SelMemory_2(m_02), .SelMemory_1(m_01),
    .SelMemory_0(m_00), .Read_Write(1'b1));  // open: Output_7, Output_6, Output_5, Output_4, Output_3, Output_2, Output_1, Output_0
  _8_bit_memories _8_bit_memories_2 (
    .Clk(d_ff_1_q), .InputBit_7(i_7), .InputBit_6(i_6), .InputBit_5(i_5), .InputBit_4(i_4), .InputBit_3(i_3),
    .InputBit_2(i_2), .InputBit_1(i_1), .InputBit_0(i_0), .SelMemory_2(m_12), .SelMemory_1(m_11),
    .SelMemory_0(m_10), .Read_Write(1'b1));  // open: Output_7, Output_6, Output_5, Output_4, Output_3, Output_2, Output_1, Output_0
  _8_bit_memories _8_bit_memories_3 (
    .Clk(d_ff_1_q), .InputBit_7(i_7), .InputBit_6(i_6), .InputBit_5(i_5), .InputBit_4(i_4), .InputBit_3(i_3),
    .InputBit_2(i_2), .InputBit_1(i_1), .InputBit_0(i_0), .SelMemory_2(m_22), .SelMemory_1(m_21),
    .SelMemory_0(m_20), .Read_Write(1'b1));  // open: Output_7, Output_6, Output_5, Output_4, Output_3, Output_2, Output_1, Output_0
  LED ClkOutput (.in(Clk));

  // Notes on the sheet:
  //   Input
endmodule
