// Digital circuit twos_complement_course.dig as structural Verilog
module twos_complement_course (
  input  s_7,
  input  s_6,
  input  s_5,
  input  s_4,
  input  s_3,
  input  s_2,
  input  s_1,
  input  s_0,
  output c_0,
  output c_1,
  output c_2,
  output c_3,
  output c_4,
  output c_5,
  output c_6,
  output c_7
);

  wire multiplexer_1_out, multiplexer_2_out, multiplexer_3_out, multiplexer_4_out, multiplexer_5_out,
       multiplexer_6_out, multiplexer_7_out, not_1_out, not_2_out, not_3_out, not_4_out, not_5_out,
       not_6_out, not_7_out;

  not not_1 (not_1_out, s_6);
  Multiplexer multiplexer_1 (.sel(s_7), .in_0(s_6), .in_1(not_1_out), .out(multiplexer_1_out));
  not not_2 (not_2_out, s_5);
  Multiplexer multiplexer_2 (.sel(s_7), .in_0(s_5), .in_1(not_2_out), .out(multiplexer_2_out));
  not not_3 (not_3_out, s_4);
  Multiplexer multiplexer_3 (.sel(s_7), .in_0(s_4), .in_1(not_3_out), .out(multiplexer_3_out));
  not not_4 (not_4_out, s_3);
  Multiplexer multiplexer_4 (.sel(s_7), .in_0(s_3), .in_1(not_4_out), .out(multiplexer_4_out));
  not not_5 (not_5_out, s_2);
  Multiplexer multiplexer_5 (.sel(s_7), .in_0(s_2), .in_1(not_5_out), .out(multiplexer_5_out));
  not not_6 (not_6_out, s_1);
  Multiplexer multiplexer_6 (.sel(s_7), .in_0(s_1), .in_1(not_6_out), .out(multiplexer_6_out));
  not not_7 (not_7_out, s_0);
  Multiplexer multiplexer_7 (.sel(s_7), .in_0(s_0), .in_1(not_7_out), .out(multiplexer_7_out));
  _8bits_adder _8bits_adder_1 (
    .a_7(1'b0), .a_6(multiplexer_1_out), .a_5(multiplexer_2_out), .a_4(multiplexer_3_out),
    .a_3(multiplexer_4_out), .a_2(multiplexer_5_out), .a_1(multiplexer_6_out), .a_0(multiplexer_7_out),
    .b_7(1'b0), .b_6(1'b0), .b_5(1'b0), .b_4(1'b0), .b_3(1'b0), .b_2(1'b0), .b_1(1'b0), .b_0(s_7), .s_6(c_6),
    .s_5(c_5), .s_4(c_4), .s_3(c_3), .s_2(c_2), .s_1(c_1), .s_0(c_0));  // open: s_7, t_7, t_6, t_5, t_4, t_3, t_2, t_1, t_0, r_1, R_1_2

  assign c_7 = s_7;

  // Notes on the sheet:
  //   Sign-magnitude representation
endmodule

/* Test case:
s_7 s_6 s_5 s_4 s_3 s_2 s_1 s_0 c_7 c_6 c_5 c_4 c_3 c_2 c_1 c_0
0   0   0   0   0   0   0   1   0   0   0   0   0   0   0   1
0   0   0   0   0   0   1   0   0   0   0   0   0   0   1   0
0   0   0   0   0   1   0   0   0   0   0   0   0   1   0   0
0   0   0   0   1   0   0   0   0   0   0   0   1   0   0   0
0   0   0   1   0   0   0   0   0   0   0   1   0   0   0   0
0   0   1   0   0   0   0   0   0   0   1   0   0   0   0   0
0   1   0   0   0   0   0   0   0   1   0   0   0   0   0   0
1   0   0   0   0   0   0   0   1   0   0   0   0   0   0   0
1   1   1   1   1   1   1   1   1   0   0   0   0   0   0   1
0   1   1   1   1   1   1   1   0   1   1   1   1   1   1   1
1   1   0   0   0   0   0   1   1   0   1   1   1   1   1   1
1   0   1   0   1   0   1   0   1   1   0   1   0   1   1   0
1   0   0   1   0   0   1   0   1   1   1   0   1   1   1   0
*/
