// Digital circuit trigger.dig as structural Verilog
module trigger (
  input  Input_0,
  input  Clk_0,
  input  Input_1,
  input  Clk_1,
  output Output_0,
  output Output_1
);

  wire d_ff_1_q, d_ff_2_q, not_1_out, not_2_out, not_3_out;

  not not_1 (not_1_out, Clk_0);
  D_FF d_ff_1 (.D(Input_0), .C(not_1_out), .Q(d_ff_1_q));  // open: nQ
  not not_2 (not_2_out, not_1_out);
  D_FF d_ff_2 (.D(Input_1), .C(Clk_1), .Q(d_ff_2_q));  // open: nQ
  not not_3 (not_3_out, Clk_1);
  D_FF d_ff_3 (.D(d_ff_1_q), .C(not_2_out), .Q(Output_0));  // open: nQ
  D_FF d_ff_4 (.D(d_ff_2_q), .C(not_3_out), .Q(Output_1));  // open: nQ
endmodule
