// Digital circuit trigger.dig as structural Verilog
module trigger (
  input  Input,
  input  Clk,
  output Output_0,
  output Output_1,
  output Output_2
);

  wire d_ff_2_q, d_ff_3_q, not_1_out, not_2_out;

  D_FF d_ff_1 (.D(Input), .C(Clk), .Q(Output_0));  // open: nQ
  D_FF d_ff_2 (.D(Input), .C(Clk), .Q(d_ff_2_q));  // open: nQ
  D_FF d_ff_3 (.D(Input), .C(not_1_out), .Q(d_ff_3_q));  // open: nQ
  not not_1 (not_1_out, Clk);
  not not_2 (not_2_out, Clk);
  D_FF d_ff_4 (.D(d_ff_2_q), .C(Clk), .Q(Output_1));  // open: nQ
  D_FF d_ff_5 (.D(d_ff_3_q), .C(not_2_out), .Q(Output_2));  // open: nQ
endmodule
